// Logisim project processor.circ as structural Verilog: 17 circuits, main circuit Adder 2 bit
module main (
);

  wire clock_1_out, control_unit_1_enable_pc, control_unit_1_jump, control_unit_1_mem_read,
       control_unit_1_mem_write, control_unit_1_next, control_unit_1_register_file_enable_reg_write;
  wire [1:0] control_unit_1_alu_operation;
  wire [3:0] control_unit_1_read_reg1, control_unit_1_read_reg2, control_unit_1_register_file_write_register;
  wire [9:0] control_unit_1_memory_address;
  wire [17:0] alu_1_result, control_unit_1_alu_input2, control_unit_1_pc_output,
       control_unit_1_register_file_input_data, control_unit_1_value_to_write, program_counter_1_pc_addr,
       ram_1_data, register_file_1_reg_data_i, register_file_1_reg_data_ii, rom_1_data;

  Clock clock_1 (.out(clock_1_out));
  RAM #(.addrWidth(10), .dataWidth(18), .bus("separate")) ram_1 (
    .addr(control_unit_1_memory_address), .din(control_unit_1_value_to_write), .data(ram_1_data),
    .str(control_unit_1_mem_write), .sel(1'b1), .clk(clock_1_out), .ld(control_unit_1_mem_read), .clr(1'b0));
  // Probe on ram_1_data
  // Probe on control_unit_1_value_to_write
  Control_Unit control_unit_1 (
    .READ_REG1(control_unit_1_read_reg1), .READ_REG2(control_unit_1_read_reg2),
    .ALU_INPUT2(control_unit_1_alu_input2), .ROM_OUTPUT(rom_1_data), .Clock(clock_1_out),
    .Memory_Address(control_unit_1_memory_address), .Value_to_Write(control_unit_1_value_to_write),
    .Data_from_RAM(ram_1_data), .MEM_WRITE(control_unit_1_mem_write), .MEM_READ(control_unit_1_mem_read),
    .Register_File_Input_Data(control_unit_1_register_file_input_data),
    .Register_File_Write_Register(control_unit_1_register_file_write_register),
    .Register_File_Enable_Reg_Write(control_unit_1_register_file_enable_reg_write),
    .REG1_Value(register_file_1_reg_data_i), .REG2_Value(register_file_1_reg_data_ii),
    .Jump(control_unit_1_jump), .Next(control_unit_1_next), .Enable_PC(control_unit_1_enable_pc),
    .ALU_OPERATION(control_unit_1_alu_operation), .ALU_OUTPUT(alu_1_result),
    .PC_OUTPUT(control_unit_1_pc_output));
  // Probe on control_unit_1_register_file_input_data
  Register_File register_file_1 (
    .Write_Data(control_unit_1_register_file_input_data),
    .Write_Register(control_unit_1_register_file_write_register), .Read_Register_I(control_unit_1_read_reg1),
    .Read_Register_II(control_unit_1_read_reg2), .Reg_Write(control_unit_1_register_file_enable_reg_write),
    .Clock(clock_1_out), .Reg_Data_I(register_file_1_reg_data_i), .Reg_Data_II(register_file_1_reg_data_ii));  // open: Clear
  ROM #(.addrWidth(18), .dataWidth(18)) rom_1 (.addr(program_counter_1_pc_addr), .data(rom_1_data), .sel(1'b1));
  Program_Counter program_counter_1 (
    .PC_IN(control_unit_1_pc_output), .JUMP(control_unit_1_jump), .NEXT(control_unit_1_next),
    .ENABLE_PC(control_unit_1_enable_pc), .CLOCK(clock_1_out), .PC_ADDR(program_counter_1_pc_addr));  // open: PC_Reset
  // Probe on register_file_1_reg_data_i
  // Probe on register_file_1_reg_data_ii
  ALU alu_1 (
    .A(register_file_1_reg_data_i), .B(control_unit_1_alu_input2), .result(alu_1_result),
    .ALU_Operation(control_unit_1_alu_operation));  // open: carry_out
  // Probe on alu_1_result

  // Notes on the sheet:
  //   Memory
  //   Instruction Memory
  //   contents of rom_1 (hex, n*v repeats v):
  //   18003 18445 28044 18002 34001 3c002 3fffd 8004 38001
endmodule

module Program_Counter (
  input  CLOCK,
  input  PC_Reset,
  input  [17:0] PC_IN,
  input  JUMP,
  input  NEXT,
  input  ENABLE_PC,
  output [17:0] PC_ADDR
);

  wire controlled_buffer_1_out, multiplexer_1_out, or_1_out;

  // Probe on PC_IN
  assign controlled_buffer_1_out = ENABLE_PC ? multiplexer_1_out : 1'bz;  // Controlled_Buffer controlled_buffer_1
  or or_1 (or_1_out, NEXT, JUMP);
  Multiplexer #(.enable("false")) multiplexer_1 (.in0(1'b0), .in1(CLOCK), .out(multiplexer_1_out), .sel(or_1_out));
  Counter counter_1 (
    .NEXT(NEXT), .JUMP(JUMP), .CLOCK(controlled_buffer_1_out), .\input (PC_IN), .reset(PC_Reset),
    .\output (PC_ADDR));
endmodule

module Register_File (
  input  [17:0] Write_Data,
  input  [3:0] Write_Register,
  input  [3:0] Read_Register_I,
  input  [3:0] Read_Register_II,
  input  Reg_Write,
  input  Clear,
  input  Clock,
  output [17:0] Reg_Data_I,
  output [17:0] Reg_Data_II
);

  wire and_1_out, and_2_out, and_3_out, and_4_out, and_5_out, and_6_out, and_7_out, and_8_out, and_9_out,
       and_10_out, and_11_out, and_12_out, and_13_out, and_14_out, and_15_out, and_16_out, decoder_1_out0,
       decoder_1_out1, decoder_1_out2, decoder_1_out3, decoder_1_out4, decoder_1_out5, decoder_1_out6,
       decoder_1_out7, decoder_1_out8, decoder_1_out9, decoder_1_out10, decoder_1_out11, decoder_1_out12,
       decoder_1_out13, decoder_1_out14, decoder_1_out15;
  wire [17:0] R0_q, R1_q, R2_q, R3_q, R4_q, R5_q, R6_q, R7_q, R8_q, R9_q, R10_q, R11_q, R12_q, R13_q, R14_q,
       R15_q;

  Decoder #(.select(4), .enable("false")) decoder_1 (
    .out0(decoder_1_out0), .out1(decoder_1_out1), .out2(decoder_1_out2), .out3(decoder_1_out3),
    .out4(decoder_1_out4), .out5(decoder_1_out5), .out6(decoder_1_out6), .out7(decoder_1_out7),
    .out8(decoder_1_out8), .out9(decoder_1_out9), .out10(decoder_1_out10), .out11(decoder_1_out11),
    .out12(decoder_1_out12), .out13(decoder_1_out13), .out14(decoder_1_out14), .out15(decoder_1_out15),
    .sel(Write_Register));
  // Probe on Write_Data
  and and_1 (and_1_out, decoder_1_out0, Reg_Write);
  Register #(.width(18)) R0 (.D(Write_Data), .en(and_1_out), .Q(R0_q), .clk(Clock), .clr(Clear));
  and and_2 (and_2_out, decoder_1_out8, Reg_Write);
  Register #(.width(18)) R8 (.D(Write_Data), .en(and_2_out), .Q(R8_q), .clk(Clock), .clr(Clear));
  and and_3 (and_3_out, decoder_1_out1, Reg_Write);
  Register #(.width(18)) R1 (.D(Write_Data), .en(and_3_out), .Q(R1_q), .clk(Clock), .clr(Clear));
  and and_4 (and_4_out, decoder_1_out9, Reg_Write);
  Register #(.width(18)) R9 (.D(Write_Data), .en(and_4_out), .Q(R9_q), .clk(Clock), .clr(Clear));
  and and_5 (and_5_out, decoder_1_out2, Reg_Write);
  Register #(.width(18)) R2 (.D(Write_Data), .en(and_5_out), .Q(R2_q), .clk(Clock), .clr(Clear));
  and and_6 (and_6_out, decoder_1_out10, Reg_Write);
  Register #(.width(18)) R10 (.D(Write_Data), .en(and_6_out), .Q(R10_q), .clk(Clock), .clr(Clear));
  and and_7 (and_7_out, decoder_1_out3, Reg_Write);
  Register #(.width(18)) R3 (.D(Write_Data), .en(and_7_out), .Q(R3_q), .clk(Clock), .clr(Clear));
  and and_8 (and_8_out, decoder_1_out11, Reg_Write);
  Register #(.width(18)) R11 (.D(Write_Data), .en(and_8_out), .Q(R11_q), .clk(Clock), .clr(Clear));
  Register #(.width(18)) R4 (.D(Write_Data), .en(and_9_out), .Q(R4_q), .clk(Clock), .clr(Clear));
  and and_9 (and_9_out, decoder_1_out4, Reg_Write);
  and and_10 (and_10_out, decoder_1_out12, Reg_Write);
  Register #(.width(18)) R12 (.D(Write_Data), .en(and_10_out), .Q(R12_q), .clk(Clock), .clr(Clear));
  and and_11 (and_11_out, decoder_1_out5, Reg_Write);
  Register #(.width(18)) R5 (.D(Write_Data), .en(and_11_out), .Q(R5_q), .clk(Clock), .clr(Clear));
  and and_12 (and_12_out, decoder_1_out13, Reg_Write);
  Register #(.width(18)) R13 (.D(Write_Data), .en(and_12_out), .Q(R13_q), .clk(Clock), .clr(Clear));
  and and_13 (and_13_out, decoder_1_out6, Reg_Write);
  Register #(.width(18)) R6 (.D(Write_Data), .en(and_13_out), .Q(R6_q), .clk(Clock), .clr(Clear));
  and and_14 (and_14_out, decoder_1_out14, Reg_Write);
  Register #(.width(18)) R14 (.D(Write_Data), .en(and_14_out), .Q(R14_q), .clk(Clock), .clr(Clear));
  Register #(.width(18)) R7 (.D(Write_Data), .en(and_15_out), .Q(R7_q), .clk(Clock), .clr(Clear));
  and and_15 (and_15_out, decoder_1_out7, Reg_Write);
  and and_16 (and_16_out, decoder_1_out15, Reg_Write);
  Register #(.width(18)) R15 (.D(Write_Data), .en(and_16_out), .Q(R15_q), .clk(Clock), .clr(Clear));
  // Probe on Reg_Data_I
  // Probe on Reg_Data_II
  Multiplexer #(.select(4), .width(18)) multiplexer_1 (
    .in0(R0_q), .in1(R1_q), .in2(R2_q), .in3(R3_q), .in4(R4_q), .in5(R5_q), .in6(R6_q), .in7(R7_q),
    .in8(R8_q), .in9(R9_q), .in10(R10_q), .in11(R11_q), .in12(R12_q), .in13(R13_q), .in14(R14_q),
    .in15(R15_q), .out(Reg_Data_I), .sel(Read_Register_I));  // open: en
  Multiplexer #(.select(4), .width(18)) multiplexer_2 (
    .in0(R0_q), .in1(R1_q), .in2(R2_q), .in3(R3_q), .in4(R4_q), .in5(R5_q), .in6(R6_q), .in7(R7_q),
    .in8(R8_q), .in9(R9_q), .in10(R10_q), .in11(R11_q), .in12(R12_q), .in13(R13_q), .in14(R14_q),
    .in15(R15_q), .out(Reg_Data_II), .sel(Read_Register_II));  // open: en
endmodule

module Instruction_Decoder (
  input  [17:0] Instruction,
  output [3:0] SRC_DST_OP1,
  output [13:0] PCOffset14,
  output [9:0] ADDR10,
  output [3:0] SRC1_OP2,
  output [3:0] SRC2,
  output [5:0] imm6_PCOffset6,
  output [6:0] ADDR7,
  output IS_IMM,
  output [4:0] BRANCH,
  output IS_CMP,
  output [1:0] ALU_Operation,
  output MEM_WRITE,
  output MEM_READ,
  output IS_JUMP,
  output IS_ALU,
  output ENABLE_REG_WRITE
);

  wire ADD, ADDI, AND, ANDI, OR, or_4_out, or_5_out, or_6_out, or_7_out, ORI, XOR, XORI;

  or or_1 (IS_IMM, ADDI, ANDI, ORI, XORI);
  or or_2 (IS_CMP, BRANCH[4], BRANCH[3], BRANCH[2], BRANCH[0], BRANCH[1]);
  or or_3 (ENABLE_REG_WRITE, IS_ALU, MEM_READ);
  Decoder #(.select(4)) decoder_1 (
    .out0(AND), .out1(OR), .out2(ADD), .out3(XOR), .out4(ANDI), .out5(ORI), .out6(ADDI), .out7(XORI),
    .out8(BRANCH[4]), .out9(BRANCH[2]), .out10(BRANCH[3]), .out11(BRANCH[0]), .out12(BRANCH[1]),
    .out13(MEM_WRITE), .out14(MEM_READ), .out15(IS_JUMP), .sel(Instruction[17:14]), .en(1'b1));
  or or_4 (or_4_out, ADD, ADDI);
  or or_5 (or_5_out, AND, ANDI);
  or or_6 (or_6_out, OR, ORI);
  or or_7 (or_7_out, XOR, XORI);
  Priority_Encoder #(.select(2)) priority_encoder_1 (
    .in0(or_4_out), .in1(or_5_out), .in2(or_6_out), .in3(or_7_out), .out(ALU_Operation));  // open: gs, en_out, en_in
  or or_8 (IS_ALU, or_4_out, or_5_out, or_6_out, or_7_out);

  assign ADDR7 = Instruction[6:0];
  assign ADDR10 = Instruction[9:0];
  assign imm6_PCOffset6 = Instruction[5:0];
  assign PCOffset14 = Instruction[13:0];
  assign SRC1_OP2 = Instruction[9:6];
  assign SRC2 = Instruction[5:2];
  assign SRC_DST_OP1 = Instruction[13:10];

  // Other names for the same wires on the sheet: imm6[5:0] = Instruction[5:0]; PCOffset6[5:0] = Instruction[5:0];
  //   OP2[3:0] = Instruction[9:6]; SRC1[3:0] = Instruction[9:6]; p = Instruction[7]; z = Instruction[8];
  //   n = Instruction[9]; ALU_CONTROL = IS_ALU; BGE = BRANCH[0]; BLE = BRANCH[1]; BGT = BRANCH[2]; BLT = BRANCH[3];
  //   BEQ = BRANCH[4]; OPCODE[3:0] = Instruction[17:14]; JUMP = IS_JUMP; LD = MEM_READ; DST[3:0] = Instruction[13:10];
  //   OP1[3:0] = Instruction[13:10]; SRC[3:0] = Instruction[13:10]; ST = MEM_WRITE
endmodule

module Control_Unit (
  input  [17:0] ROM_OUTPUT,
  input  [17:0] REG1_Value,
  input  [17:0] REG2_Value,
  input  Clock,
  input  [17:0] Data_from_RAM,
  input  [17:0] ALU_OUTPUT,
  output [17:0] Register_File_Input_Data,
  output [3:0] READ_REG1,
  output [3:0] READ_REG2,
  output Jump,
  output [3:0] Register_File_Write_Register,
  output Register_File_Enable_Reg_Write,
  output Next,
  output Enable_PC,
  output [1:0] ALU_OPERATION,
  output [17:0] PC_OUTPUT,
  output [9:0] Memory_Address,
  output [17:0] Value_to_Write,
  output MEM_READ,
  output [17:0] ALU_INPUT2,
  output MEM_WRITE
);

  wire and_1_out, and_2_out, and_3_out, and_4_out, and_5_out, and_6_out, BEQ, BGE, BGT, BLE, BLT,
       CMP_SUCCESSOR, comparator_18_bit_1_eq, comparator_18_bit_1_gt, comparator_18_bit_1_lt,
       controlled_buffer_2_out, controlled_buffer_3_out, controlled_buffer_4_out, controlled_buffer_5_out,
       controlled_buffer_6_out, counter_4_q, decoder_1_out0, decoder_1_out2, decoder_2_out1, decoder_2_out2,
       decoder_3_out0, decoder_3_out2, decoder_4_out0, decoder_4_out1, decoder_5_out1, decoder_5_out2,
       ENABLE_REG_WRITE, IS_ALU, IS_CMP, IS_IMM, IS_JUMP, JMP_BRANCH, JUMP_J, NEXT_ALU, NEXT_LD, NEXT_ST,
       or_1_out, or_2_out, REG_ALU_WRITE, REG_WRITE, REG_WRITE_LD;
  wire [1:0] counter_1_q, counter_2_q, counter_3_q, counter_5_q;
  wire [3:0] SRC1_OP2, SRC2;
  wire [5:0] imm6_PCOffset6;
  wire [6:0] ADDR7;
  wire [9:0] ADDR10, zero_extender_7to10_1_extended_value;
  wire [13:0] PCOffset14;
  wire [17:0] imm18_PCOffset18, multiplexer_6_out, REG_WRITE_DATA, sign_extender_14to18_1_out_2;

  Zero_Extender_7to10 zero_extender_7to10_1 (.Extended_Value(zero_extender_7to10_1_extended_value), .Input(ADDR7));
  Multiplexer #(.width(10), .enable("false")) multiplexer_1 (
    .in0(ADDR10), .in1(zero_extender_7to10_1_extended_value), .out(Memory_Address), .sel(MEM_WRITE));
  Instruction_Decoder instruction_decoder_1 (
    .SRC_DST_OP1(Register_File_Write_Register), .SRC1_OP2(SRC1_OP2), .SRC2(SRC2), .Instruction(ROM_OUTPUT),
    .BRANCH({BEQ, BLT, BGT, BLE, BGE}), .PCOffset14(PCOffset14), .ADDR10(ADDR10),
    .imm6_PCOffset6(imm6_PCOffset6), .ADDR7(ADDR7), .IS_IMM(IS_IMM), .IS_CMP(IS_CMP),
    .ALU_Operation(ALU_OPERATION), .MEM_WRITE(MEM_WRITE), .MEM_READ(MEM_READ), .IS_JUMP(IS_JUMP),
    .IS_ALU(IS_ALU), .ENABLE_REG_WRITE(ENABLE_REG_WRITE));
  and and_1 (and_1_out, IS_IMM, IS_ALU);
  assign REG_WRITE_DATA = IS_ALU ? ALU_OUTPUT : 18'bz;  // Controlled_Buffer controlled_buffer_1
  Sign_Extender_6to18 sign_extender_6to18_1 (.in_1(imm6_PCOffset6), .out_2(imm18_PCOffset18));
  Multiplexer #(.width(18), .enable("false")) multiplexer_2 (
    .in0(REG2_Value), .in1(imm18_PCOffset18), .out(ALU_INPUT2), .sel(and_1_out));
  Multiplexer #(.width(18), .enable("false")) multiplexer_3 (
    .in0(REG_WRITE_DATA), .in1(Data_from_RAM), .out(Register_File_Input_Data), .sel(MEM_READ));
  Multiplexer #(.enable("false")) multiplexer_4 (
    .in0(1'b0), .in1(ENABLE_REG_WRITE), .out(Register_File_Enable_Reg_Write), .sel(REG_WRITE));
  Multiplexer #(.width(4)) multiplexer_5 (
    .in0(SRC1_OP2), .in1(Register_File_Write_Register), .out(READ_REG1), .sel(IS_CMP));  // open: en
  Comparator_18_bit comparator_18_bit_1 (
    .a(REG1_Value), .b(REG2_Value), .gt(comparator_18_bit_1_gt), .lt(comparator_18_bit_1_lt),
    .eq(comparator_18_bit_1_eq));
  Multiplexer #(.width(18), .enable("false")) multiplexer_6 (
    .in0(18'h1), .in1(imm18_PCOffset18), .out(multiplexer_6_out), .sel(CMP_SUCCESSOR));
  or or_1 (or_1_out, comparator_18_bit_1_eq, comparator_18_bit_1_gt);
  or or_2 (or_2_out, comparator_18_bit_1_eq, comparator_18_bit_1_lt);
  Sign_Extender_14to18 sign_extender_14to18_1 (.in_1(PCOffset14), .out_2(sign_extender_14to18_1_out_2));
  and and_2 (and_2_out, BGE, or_1_out);
  and and_3 (and_3_out, BLE, or_2_out);
  and and_4 (and_4_out, BGT, comparator_18_bit_1_gt);
  and and_5 (and_5_out, BLT, comparator_18_bit_1_lt);
  and and_6 (and_6_out, BEQ, comparator_18_bit_1_eq);
  Multiplexer #(.width(18), .enable("false")) multiplexer_7 (
    .in0(multiplexer_6_out), .in1(sign_extender_14to18_1_out_2), .out(PC_OUTPUT), .sel(IS_JUMP));
  or or_3 (CMP_SUCCESSOR, and_2_out, and_3_out, and_4_out, and_5_out, and_6_out);
  Multiplexer #(.width(4)) multiplexer_8 (.in0(SRC2), .in1(SRC1_OP2), .out(READ_REG2), .sel(IS_CMP));  // open: en
  or or_4 (Jump, JUMP_J, JMP_BRANCH);
  or or_5 (REG_WRITE, REG_ALU_WRITE, REG_WRITE_LD);
  or or_6 (Next, NEXT_ALU, NEXT_LD, NEXT_ST);
  or or_7 (Enable_PC, NEXT_ALU, NEXT_LD, NEXT_ST, JUMP_J, JMP_BRANCH);
  assign controlled_buffer_2_out = IS_ALU ? Clock : 1'bz;  // Controlled_Buffer controlled_buffer_2
  assign controlled_buffer_3_out = IS_CMP ? Clock : 1'bz;  // Controlled_Buffer controlled_buffer_3
  assign controlled_buffer_4_out = MEM_READ ? Clock : 1'bz;  // Controlled_Buffer controlled_buffer_4
  assign controlled_buffer_5_out = MEM_WRITE ? Clock : 1'bz;  // Controlled_Buffer controlled_buffer_5
  assign controlled_buffer_6_out = IS_JUMP ? Clock : 1'bz;  // Controlled_Buffer controlled_buffer_6
  Decoder #(.select(2)) decoder_1 (
    .out0(decoder_1_out0), .out1(REG_ALU_WRITE), .out2(decoder_1_out2), .sel(counter_1_q));  // open: out3, en
  Counter_part #(.width(2), .max('h2)) counter_1 (
    .Q(counter_1_q), .clk(controlled_buffer_2_out));  // open: load, D, count, carry, clr
  Decoder #(.select(2), .enable("false")) decoder_2 (
    .out1(decoder_2_out1), .out2(decoder_2_out2), .sel(counter_2_q));  // open: out0, out3
  Counter_part #(.width(2), .max('h2)) counter_2 (
    .Q(counter_2_q), .clk(controlled_buffer_3_out));  // open: load, D, count, carry, clr
  Decoder #(.select(2), .enable("false")) decoder_3 (
    .out0(decoder_3_out0), .out1(REG_WRITE_LD), .out2(decoder_3_out2), .sel(counter_3_q));  // open: out3
  Counter_part #(.width(2), .max('h2)) counter_3 (
    .Q(counter_3_q), .clk(controlled_buffer_4_out));  // open: load, D, count, carry, clr
  Decoder #(.enable("false")) decoder_4 (.out0(decoder_4_out0), .out1(decoder_4_out1), .sel(counter_4_q));
  Counter_part #(.width(1), .max('h1)) counter_4 (
    .Q(counter_4_q), .clk(controlled_buffer_5_out));  // open: load, D, count, carry, clr
  Decoder #(.select(2), .enable("false")) decoder_5 (
    .out1(decoder_5_out1), .out2(decoder_5_out2), .out3(decoder_5_out2), .sel(counter_5_q));  // open: out0
  Counter_part #(.width(2), .max('h2)) counter_5 (
    .Q(counter_5_q), .clk(controlled_buffer_6_out));  // open: load, D, count, carry, clr
  assign NEXT_ALU = decoder_1_out0 ? 1'b0 : 1'bz;  // Controlled_Buffer controlled_buffer_7
  assign NEXT_ALU = decoder_1_out2 ? 1'b1 : 1'bz;  // Controlled_Buffer controlled_buffer_8
  assign JMP_BRANCH = decoder_2_out1 ? 1'b1 : 1'bz;  // Controlled_Buffer controlled_buffer_9
  assign JMP_BRANCH = decoder_2_out2 ? 1'b0 : 1'bz;  // Controlled_Buffer controlled_buffer_10
  assign NEXT_LD = decoder_3_out0 ? 1'b0 : 1'bz;  // Controlled_Buffer controlled_buffer_11
  assign NEXT_LD = decoder_3_out2 ? 1'b1 : 1'bz;  // Controlled_Buffer controlled_buffer_12
  assign NEXT_ST = decoder_4_out0 ? 1'b0 : 1'bz;  // Controlled_Buffer controlled_buffer_13
  assign NEXT_ST = decoder_4_out1 ? 1'b1 : 1'bz;  // Controlled_Buffer controlled_buffer_14
  assign JUMP_J = decoder_5_out1 ? 1'b1 : 1'bz;  // Controlled_Buffer controlled_buffer_15
  assign JUMP_J = decoder_5_out2 ? 1'b0 : 1'bz;  // Controlled_Buffer controlled_buffer_16

  assign Value_to_Write = REG2_Value;

  // Other names for the same wires on the sheet: BRANCH[4:0] = {BEQ, BLT, BGT, BLE, BGE};
  //   MEM_DATA[17:0] = Data_from_RAM; PC_ALU_ENABLE = NEXT_ALU; PC_BRANCH_ENABLE = JMP_BRANCH;
  //   PC_JUMP_ENABLE = JUMP_J; PC_LD_ENABLE = NEXT_LD; PC_ST_ENABLE = NEXT_ST; REG1_VAL[17:0] = REG1_Value;
  //   REG2_VAL[17:0] = REG2_Value; SRC_DST_OP1[3:0] = Register_File_Write_Register

  // Notes on the sheet:
  //   Memory Management
  //   Decode Instruction
  //   ALU Management
  //   Register File Management
  //   Program Counter Management
  //   State Management
  //   ALU
  //   BRANCH
  //   LD
  //   ST
  //   JUMP
endmodule

module ALU (
  input  [17:0] A,
  input  [17:0] B,
  input  [1:0] ALU_Operation,
  output carry_out,
  output [17:0] result
);

  wire [17:0] adder_18_bit_1_sum, AND_out, OR_out, XOR_out;

  Adder_18_bit adder_18_bit_1 (.A(A), .B(B), .carry_in(1'b0), .sum(adder_18_bit_1_sum), .carry_out(carry_out));
  assign AND_out = B & A;  // AND_Gate AND, 18 bits wide
  assign OR_out = B | A;  // OR_Gate OR, 18 bits wide
  assign XOR_out = A ^ B;  // XOR_Gate XOR, 18 bits wide
  Multiplexer #(.select(2), .width(18), .enable("false")) multiplexer_1 (
    .in0(adder_18_bit_1_sum), .in1(AND_out), .in2(OR_out), .in3(XOR_out), .out(result), .sel(ALU_Operation));
endmodule

module Counter (
  input  NEXT,
  input  JUMP,
  input  CLOCK,
  input  [17:0] \input ,
  input  reset,
  output [17:0] \output 
);

  wire ENABLE_LOAD, not_1_out, or_1_out;
  wire [17:0] inverter_18_bit_1_out_2, LOAD_VAL, VAL_ADDED, VAL_SUBTRACTED;

  not not_1 (not_1_out, NEXT);
  or or_1 (or_1_out, JUMP, \input [17]);
  and and_1 (ENABLE_LOAD, not_1_out, or_1_out);
  Counter_part #(.width(18), .max('h3ffff)) counter_1 (
    .load(ENABLE_LOAD), .D(LOAD_VAL), .count(NEXT), .Q(\output ), .clk(CLOCK), .clr(reset));  // open: carry
  Inverter_18_bit inverter_18_bit_1 (.in_1(\input ), .out_2(inverter_18_bit_1_out_2));
  Adder #(.width(18)) adder_1 (.a(\input ), .b(\output ), .out(VAL_ADDED));  // open: cin, cout
  Subtractor #(.width(18)) subtractor_1 (
    .a(\output ), .b(inverter_18_bit_1_out_2), .out(VAL_SUBTRACTED));  // open: bin, bout
  assign LOAD_VAL = JUMP ? VAL_ADDED : 18'bz;  // Controlled_Buffer controlled_buffer_1
  assign LOAD_VAL = \input [17] ? VAL_SUBTRACTED : 18'bz;  // Controlled_Buffer controlled_buffer_2

  // Other names for the same wires on the sheet: count = NEXT; SUBTRACT = \input [17]
endmodule

module Half_Comparator (
  input  A,
  input  B,
  output gt,
  output lt,
  output eq
);

  wire and_1_out, and_4_out, not_1_out, not_2_out, not_3_out, not_4_out;

  not not_1 (not_1_out, A);
  and and_1 (and_1_out, not_1_out, not_2_out);
  not not_2 (not_2_out, B);
  and and_2 (gt, A, not_3_out);
  not not_3 (not_3_out, B);
  not not_4 (not_4_out, A);
  and and_3 (lt, not_4_out, B);
  and and_4 (and_4_out, A, B);
  or or_1 (eq, and_4_out, and_1_out);
endmodule

module Full_Comparator (
  input  a,
  input  b,
  input  gt_in,
  input  lt_in,
  input  eq_in,
  output gt,
  output lt,
  output eq
);

  wire and_1_out, and_2_out, and_3_out, and_4_out, not_1_out, not_2_out, not_3_out, not_4_out, or_3_out;

  and and_1 (and_1_out, a, not_1_out, eq_in);
  not not_1 (not_1_out, b);
  not not_2 (not_2_out, a);
  and and_2 (and_2_out, not_2_out, b, eq_in);
  and and_3 (and_3_out, a, b);
  not not_3 (not_3_out, a);
  and and_4 (and_4_out, not_3_out, not_4_out);
  not not_4 (not_4_out, b);
  or or_1 (gt, and_1_out, gt_in);
  or or_2 (lt, and_2_out, lt_in);
  or or_3 (or_3_out, and_3_out, and_4_out);
  and and_5 (eq, eq_in, or_3_out);
endmodule

module Full_Adder (
  input  A,
  input  B,
  input  carry_in,
  output sum,
  output carry_out
);

  wire and_1_out, and_2_out, xor_1_out, xor_2_out;

  xor xor_1 (xor_1_out, A, B);
  xor xor_2 (xor_2_out, A, B);
  xor xor_3 (sum, xor_1_out, carry_in);
  and and_1 (and_1_out, carry_in, xor_2_out);
  and and_2 (and_2_out, B, A);
  or or_1 (carry_out, and_1_out, and_2_out);
endmodule

module Sign_Extender_6to18 (
  input  [5:0] in_1,
  output [17:0] out_2
);

  Multiplexer #(.width(12), .enable("false")) multiplexer_1 (
    .in0({12{1'b0}}), .in1({12{1'b1}}), .out(out_2[17:6]), .sel(in_1[5]));

  assign out_2[5:0] = in_1;
endmodule

module Sign_Extender_14to18 (
  input  [13:0] in_1,
  output [17:0] out_2
);

  Multiplexer #(.width(4), .enable("false")) multiplexer_1 (
    .in0(4'b0000), .in1(4'b1111), .out(out_2[17:14]), .sel(in_1[13]));

  assign out_2[13:0] = in_1;
endmodule

module Zero_Extender_7to10 (
  input  [6:0] Input,
  output [9:0] Extended_Value
);


  assign Extended_Value = {3'b000, Input};
endmodule

module Comparator_18_bit (
  input  [17:0] a,
  input  [17:0] b,
  output gt,
  output lt,
  output eq
);

  wire full_comparator_1_eq, full_comparator_1_gt, full_comparator_1_lt, full_comparator_2_eq,
       full_comparator_2_gt, full_comparator_2_lt, full_comparator_3_eq, full_comparator_3_gt,
       full_comparator_3_lt, full_comparator_4_eq, full_comparator_4_gt, full_comparator_4_lt,
       full_comparator_5_eq, full_comparator_5_gt, full_comparator_5_lt, full_comparator_6_eq,
       full_comparator_6_gt, full_comparator_6_lt, full_comparator_7_eq, full_comparator_7_gt,
       full_comparator_7_lt, full_comparator_8_eq, full_comparator_8_gt, full_comparator_8_lt,
       full_comparator_9_eq, full_comparator_9_gt, full_comparator_9_lt, full_comparator_10_eq,
       full_comparator_10_gt, full_comparator_10_lt, full_comparator_11_eq, full_comparator_11_gt,
       full_comparator_11_lt, full_comparator_12_eq, full_comparator_12_gt, full_comparator_12_lt,
       full_comparator_13_eq, full_comparator_13_gt, full_comparator_13_lt, full_comparator_14_eq,
       full_comparator_14_gt, full_comparator_14_lt, full_comparator_15_eq, full_comparator_15_gt,
       full_comparator_15_lt, full_comparator_16_eq, full_comparator_16_gt, full_comparator_16_lt,
       half_comparator_1_eq, half_comparator_1_gt, half_comparator_1_lt;

  Half_Comparator half_comparator_1 (
    .A(a[17]), .B(b[17]), .gt(half_comparator_1_gt), .lt(half_comparator_1_lt), .eq(half_comparator_1_eq));
  Full_Comparator full_comparator_1 (
    .a(a[8]), .b(b[8]), .gt_in(full_comparator_16_gt), .lt_in(full_comparator_16_lt),
    .eq_in(full_comparator_16_eq), .gt(full_comparator_1_gt), .lt(full_comparator_1_lt),
    .eq(full_comparator_1_eq));
  Full_Comparator full_comparator_2 (
    .a(a[16]), .b(b[16]), .gt_in(half_comparator_1_gt), .lt_in(half_comparator_1_lt),
    .eq_in(half_comparator_1_eq), .gt(full_comparator_2_gt), .lt(full_comparator_2_lt),
    .eq(full_comparator_2_eq));
  Full_Comparator full_comparator_3 (
    .a(a[7]), .b(b[7]), .gt_in(full_comparator_1_gt), .lt_in(full_comparator_1_lt),
    .eq_in(full_comparator_1_eq), .gt(full_comparator_3_gt), .lt(full_comparator_3_lt),
    .eq(full_comparator_3_eq));
  Full_Comparator full_comparator_4 (
    .a(a[15]), .b(b[15]), .gt_in(full_comparator_2_gt), .lt_in(full_comparator_2_lt),
    .eq_in(full_comparator_2_eq), .gt(full_comparator_4_gt), .lt(full_comparator_4_lt),
    .eq(full_comparator_4_eq));
  Full_Comparator full_comparator_5 (
    .a(a[14]), .b(b[14]), .gt_in(full_comparator_4_gt), .lt_in(full_comparator_4_lt),
    .eq_in(full_comparator_4_eq), .gt(full_comparator_5_gt), .lt(full_comparator_5_lt),
    .eq(full_comparator_5_eq));
  Full_Comparator full_comparator_6 (
    .a(a[6]), .b(b[6]), .gt_in(full_comparator_3_gt), .lt_in(full_comparator_3_lt),
    .eq_in(full_comparator_3_eq), .gt(full_comparator_6_gt), .lt(full_comparator_6_lt),
    .eq(full_comparator_6_eq));
  Full_Comparator full_comparator_7 (
    .a(a[13]), .b(b[13]), .gt_in(full_comparator_5_gt), .lt_in(full_comparator_5_lt),
    .eq_in(full_comparator_5_eq), .gt(full_comparator_7_gt), .lt(full_comparator_7_lt),
    .eq(full_comparator_7_eq));
  Full_Comparator full_comparator_8 (
    .a(a[5]), .b(b[5]), .gt_in(full_comparator_6_gt), .lt_in(full_comparator_6_lt),
    .eq_in(full_comparator_6_eq), .gt(full_comparator_8_gt), .lt(full_comparator_8_lt),
    .eq(full_comparator_8_eq));
  Full_Comparator full_comparator_9 (
    .a(a[12]), .b(b[12]), .gt_in(full_comparator_7_gt), .lt_in(full_comparator_7_lt),
    .eq_in(full_comparator_7_eq), .gt(full_comparator_9_gt), .lt(full_comparator_9_lt),
    .eq(full_comparator_9_eq));
  Full_Comparator full_comparator_10 (
    .a(a[4]), .b(b[4]), .gt_in(full_comparator_8_gt), .lt_in(full_comparator_8_lt),
    .eq_in(full_comparator_8_eq), .gt(full_comparator_10_gt), .lt(full_comparator_10_lt),
    .eq(full_comparator_10_eq));
  Full_Comparator full_comparator_11 (
    .a(a[11]), .b(b[11]), .gt_in(full_comparator_9_gt), .lt_in(full_comparator_9_lt),
    .eq_in(full_comparator_9_eq), .gt(full_comparator_11_gt), .lt(full_comparator_11_lt),
    .eq(full_comparator_11_eq));
  Full_Comparator full_comparator_12 (
    .a(a[3]), .b(b[3]), .gt_in(full_comparator_10_gt), .lt_in(full_comparator_10_lt),
    .eq_in(full_comparator_10_eq), .gt(full_comparator_12_gt), .lt(full_comparator_12_lt),
    .eq(full_comparator_12_eq));
  Full_Comparator full_comparator_13 (
    .a(a[10]), .b(b[10]), .gt_in(full_comparator_11_gt), .lt_in(full_comparator_11_lt),
    .eq_in(full_comparator_11_eq), .gt(full_comparator_13_gt), .lt(full_comparator_13_lt),
    .eq(full_comparator_13_eq));
  Full_Comparator full_comparator_14 (
    .a(a[2]), .b(b[2]), .gt_in(full_comparator_12_gt), .lt_in(full_comparator_12_lt),
    .eq_in(full_comparator_12_eq), .gt(full_comparator_14_gt), .lt(full_comparator_14_lt),
    .eq(full_comparator_14_eq));
  Full_Comparator full_comparator_15 (
    .a(a[1]), .b(b[1]), .gt_in(full_comparator_14_gt), .lt_in(full_comparator_14_lt),
    .eq_in(full_comparator_14_eq), .gt(full_comparator_15_gt), .lt(full_comparator_15_lt),
    .eq(full_comparator_15_eq));
  Full_Comparator full_comparator_16 (
    .a(a[9]), .b(b[9]), .gt_in(full_comparator_13_gt), .lt_in(full_comparator_13_lt),
    .eq_in(full_comparator_13_eq), .gt(full_comparator_16_gt), .lt(full_comparator_16_lt),
    .eq(full_comparator_16_eq));
  Full_Comparator full_comparator_17 (
    .a(a[0]), .b(b[0]), .gt_in(full_comparator_15_gt), .lt_in(full_comparator_15_lt),
    .eq_in(full_comparator_15_eq), .gt(gt), .lt(lt), .eq(eq));
endmodule

module Inverter_18_bit (
  input  [17:0] in_1,
  output [17:0] out_2
);

  wire [17:0] negator_1_out;

  Negator #(.width(18)) negator_1 (.in(in_1), .out(negator_1_out));
  Multiplexer #(.width(18)) multiplexer_1 (.in0(in_1), .in1(negator_1_out), .out(out_2), .sel(in_1[17]));  // open: en
endmodule

module Adder_18_bit (
  input  [17:0] A,
  input  [17:0] B,
  input  carry_in,
  output carry_out,
  output [17:0] sum
);

  wire adder_2_bit_1_carry_out, adder_2_bit_2_carry_out, adder_2_bit_3_carry_out, adder_2_bit_4_carry_out,
       adder_2_bit_5_carry_out, adder_2_bit_6_carry_out, adder_2_bit_7_carry_out, adder_2_bit_8_carry_out;

  Adder_2_bit adder_2_bit_1 (
    .A(A[1:0]), .B(B[1:0]), .carry_in(carry_in), .carry_out(adder_2_bit_1_carry_out), .sum(sum[1:0]));
  Adder_2_bit adder_2_bit_2 (
    .A(A[3:2]), .B(B[3:2]), .carry_in(adder_2_bit_1_carry_out), .carry_out(adder_2_bit_2_carry_out),
    .sum(sum[3:2]));
  Adder_2_bit adder_2_bit_3 (
    .A(A[5:4]), .B(B[5:4]), .carry_in(adder_2_bit_2_carry_out), .carry_out(adder_2_bit_3_carry_out),
    .sum(sum[5:4]));
  Adder_2_bit adder_2_bit_4 (
    .A(A[7:6]), .B(B[7:6]), .carry_in(adder_2_bit_3_carry_out), .carry_out(adder_2_bit_4_carry_out),
    .sum(sum[7:6]));
  Adder_2_bit adder_2_bit_5 (
    .A(A[9:8]), .B(B[9:8]), .carry_in(adder_2_bit_4_carry_out), .carry_out(adder_2_bit_5_carry_out),
    .sum(sum[9:8]));
  Adder_2_bit adder_2_bit_6 (
    .A(A[11:10]), .B(B[11:10]), .carry_in(adder_2_bit_5_carry_out), .carry_out(adder_2_bit_6_carry_out),
    .sum(sum[11:10]));
  Adder_2_bit adder_2_bit_7 (
    .A(A[13:12]), .B(B[13:12]), .carry_in(adder_2_bit_6_carry_out), .carry_out(adder_2_bit_7_carry_out),
    .sum(sum[13:12]));
  Adder_2_bit adder_2_bit_8 (
    .A(A[15:14]), .B(B[15:14]), .carry_in(adder_2_bit_7_carry_out), .carry_out(adder_2_bit_8_carry_out),
    .sum(sum[15:14]));
  Adder_2_bit adder_2_bit_9 (
    .A(A[17:16]), .B(B[17:16]), .carry_in(adder_2_bit_8_carry_out), .carry_out(carry_out), .sum(sum[17:16]));
endmodule

module Adder_2_bit (
  input  [1:0] A,
  input  [1:0] B,
  input  carry_in,
  output carry_out,
  output [1:0] sum
);

  wire full_adder_1_carry_out;

  Full_Adder full_adder_1 (.A(A[0]), .B(B[0]), .carry_in(carry_in), .sum(sum[0]), .carry_out(full_adder_1_carry_out));
  Full_Adder full_adder_2 (.A(A[1]), .B(B[1]), .carry_in(full_adder_1_carry_out), .sum(sum[1]), .carry_out(carry_out));
endmodule
