// Logisim project bird.circ as structural Verilog: 16 circuits, main circuit main
module main (
  input  [15:0] Datain,
  output [15:0] Dout,
  output [11:0] Addrout,
  output clk,
  output memld
);

  wire ALU_zero, datamux, irld, mux, pcinc, pcld, pcmux, regld, sp_minus_minus, sp_plus_plus, zf, zfld;
  wire [1:0] armux;
  wire [2:0] dst, src1, src2;
  wire [3:0] registerbank_1_dout1, registerbank_1_dout1_2, registerbank_1_dout1_3, registerbank_1_dout1_4;
  wire [5:0] opcode;
  wire [11:0] adder_1_out, alu2_12, IR_addr, multiplexer_2_out, PC_output, R7_12;
  wire [15:0] ALU_aluresult, bit_extender_1_out, multiplexer_4_out, multiplexer_5_out, registerbank_1_dout2,
       registerbank_1_dout3, registerbank_1_dout4, registerbank_1_dout5, registerbank_1_dout6,
       registerbank_1_dout7;
  wire [15:12] alu2_16, R7_16;
  wire [17:0] Control_Unit_out_4;

  Clock clock_1 (.out(clk));
  Adder #(.width(12)) adder_1 (.a(PC_output), .b(IR_addr), .out(adder_1_out));  // open: cin, cout
  Multiplexer #(.select(2), .width(12), .enable("false")) multiplexer_1 (
    .in0(PC_output), .in1(alu2_12), .in2(R7_12), .out(Addrout), .sel(armux));  // open: in3
  PC PC (.pc_load(pcld), .clock(clk), .\output (PC_output), .increment(pcinc), .input_data(multiplexer_2_out));
  Multiplexer #(.width(12), .enable("false")) multiplexer_2 (
    .in0(adder_1_out), .in1(Datain[11:0]), .out(multiplexer_2_out), .sel(pcmux));
  Multiplexer #(.width(16), .enable("false")) multiplexer_3 (
    .in0(multiplexer_5_out), .in1(bit_extender_1_out), .out(Dout), .sel(datamux));
  assign bit_extender_1_out = {{4{1'b0}}, PC_output};  // Bit_Extender bit_extender_1
  RAM #(.addrWidth(12), .dataWidth(16), .bus("separate")) ram_1 ();  // open: addr, din, data, str, sel, clk, ld, clr
  Registerbank registerbank_1 (
    .Reg_Select(dst), .Reg_load(regld), .Data_In(multiplexer_4_out),
    .DOUT1({registerbank_1_dout1_4, registerbank_1_dout1_3, registerbank_1_dout1_2, registerbank_1_dout1}),
    .DOUT2(registerbank_1_dout2), .DOUT3(registerbank_1_dout3), .DOUT4(registerbank_1_dout4),
    .DOUT5(registerbank_1_dout5), .DOUT6(registerbank_1_dout6), .DOUT7(registerbank_1_dout7),
    .DOUT8({R7_16, R7_12}), .clock(clk), .sp_increment(sp_plus_plus), .sp_decrement(sp_minus_minus));
  _1_bit_Register u_ZF (.Data(ALU_zero), .Output(zf), .Load(zfld), .clk(clk));
  Multiplexer #(.width(16), .enable("false")) multiplexer_4 (
    .in0(ALU_aluresult), .in1(Datain), .out(multiplexer_4_out), .sel(mux));
  Multiplexer #(.select(3), .width(16), .enable("false")) multiplexer_5 (
    .in0({registerbank_1_dout1_4, registerbank_1_dout1_3, registerbank_1_dout1_2, registerbank_1_dout1}),
    .in1(registerbank_1_dout2), .in2(registerbank_1_dout3), .in3(registerbank_1_dout4),
    .in4(registerbank_1_dout5), .in5(registerbank_1_dout6), .in6(registerbank_1_dout7), .in7({R7_16, R7_12}),
    .out(multiplexer_5_out), .sel(src1));
  ALU ALU (.A(multiplexer_5_out), .B({alu2_16, alu2_12}), .AluOp(opcode), .AluResult(ALU_aluresult), .Zero(ALU_zero));
  Multiplexer #(.select(3), .width(16), .enable("false")) multiplexer_6 (
    .in0({registerbank_1_dout1_4, registerbank_1_dout1_3, registerbank_1_dout1_2, registerbank_1_dout1}),
    .in1(registerbank_1_dout2), .in2(registerbank_1_dout3), .in3(registerbank_1_dout4),
    .in4(registerbank_1_dout5), .in5(registerbank_1_dout6), .in6(registerbank_1_dout7), .in7({R7_16, R7_12}),
    .out({alu2_16, alu2_12}), .sel(src2));
  Control_Unit Control_Unit (
    .opcode(Datain[15:12]), .ZF(zf), .clock(clk),
    .out_4({Control_Unit_out_4[17], pcmux, pcld, pcinc, armux, regld, zfld, mux, memld, irld, sp_plus_plus, sp_minus_minus, datamux, Control_Unit_out_4[3:0]}));
  Instruction_Register IR (
    .in_1(Datain[11:0]), .src1(src1), .aluop(opcode), .src2(src2), .dst(dst), .addr(IR_addr), .clock(clk),
    .load(irld));
  Hex_Digit_Display hex_digit_display_1 (.value(registerbank_1_dout1_3));  // open: dp
  Hex_Digit_Display hex_digit_display_2 (.value(registerbank_1_dout1_4));  // open: dp
  Hex_Digit_Display hex_digit_display_3 (.value(registerbank_1_dout1_2));  // open: dp
  Hex_Digit_Display hex_digit_display_4 (.value(registerbank_1_dout1));  // open: dp

  // Other names for the same wires on the sheet: alu2_16[11:0] = alu2_12; clock = clk; R7_16[11:0] = R7_12

  // Notes on the sheet:
  //   Control Signals
endmodule

module Control_Unit (
  input  [3:0] opcode,
  input  ZF,
  input  clock,
  output [17:0] out_4
);

  wire not_1_out, not_2_out, not_3_out;
  wire [1:1] and_1_out;
  wire [3:0] _4_bits_reg_out_3, multiplexer_1_out, multiplexer_2_out;

  and and_1 (and_1_out[1], not_1_out, not_2_out, opcode[2], not_3_out);
  not not_1 (not_1_out, opcode[0]);
  not not_2 (not_2_out, opcode[1]);
  not not_3 (not_3_out, opcode[3]);
  Multiplexer #(.select(2), .width(4), .enable("false")) multiplexer_1 (
    .in0(opcode), .in1(opcode), .in2(4'b0000), .in3(4'b0101), .out(multiplexer_1_out),
    .sel({and_1_out[1], ZF}));
  Multiplexer #(.width(4), .enable("false")) multiplexer_2 (
    .in0(out_4[3:0]), .in1(multiplexer_1_out), .out(multiplexer_2_out), .sel(out_4[17]));
  _4_bits_Register _4_bits_reg (.in_1(multiplexer_2_out), .in_2(clock), .out_3(_4_bits_reg_out_3));
  ROM #(.addrWidth(4), .dataWidth(18)) rom_1 (.addr(_4_bits_reg_out_3), .data(out_4));  // open: sel

  // Notes on the sheet:
  //   last 4 bits
  //   =
  //   next state to be fetched
  //   contents of rom_1 (hex, n*v repeats v):
  //   24080 4a00 11a00 1100 0 8000 0 c00 2120 4c a130 4d 2a00 1a000
endmodule

module ALU (
  input  [15:0] A,
  input  [15:0] B,
  input  [5:0] AluOp,
  output [15:0] AluResult,
  output Zero
);

  wire [15:0] adder_1_out, adder_2_out, Bitwise_And_out, Bitwise_Not_out, Bitwise_Or_out, Bitwise_Xor_out,
       multiplexer_1_out, subtractor_1_out, subtractor_2_out;

  assign Bitwise_And_out = A & B;  // AND_Gate Bitwise_And, 16 bits wide
  assign Bitwise_Or_out = A | B;  // OR_Gate Bitwise_Or, 16 bits wide
  assign Bitwise_Xor_out = A ^ B;  // XOR_Gate Bitwise_Xor, 16 bits wide
  assign Bitwise_Not_out = ~B;  // NOT_Gate Bitwise_Not, 16 bits wide
  Adder #(.width(16)) adder_1 (.a(A), .b(B), .out(adder_1_out));  // open: cin, cout
  Subtractor #(.width(16)) subtractor_1 (.a(A), .b(B), .out(subtractor_1_out));  // open: bin, bout
  Adder #(.width(16)) adder_2 (.a(B), .b(16'h1), .out(adder_2_out));  // open: cin, cout
  Subtractor #(.width(16)) subtractor_2 (.a(B), .b(16'h1), .out(subtractor_2_out));  // open: bin, bout
  Multiplexer #(.select(3), .width(16)) multiplexer_1 (
    .in0(Bitwise_Not_out), .in1(B), .in2(adder_2_out), .in3(subtractor_2_out), .out(multiplexer_1_out),
    .sel({1'b0, AluOp[1:0]}));  // open: in4, in5, in6, in7, en
  Multiplexer #(.select(3), .width(16)) multiplexer_2 (
    .in0(adder_1_out), .in1(subtractor_1_out), .in2(Bitwise_And_out), .in3(Bitwise_Or_out),
    .in4(Bitwise_Xor_out), .in7(multiplexer_1_out), .out(AluResult), .sel(AluOp[5:3]));  // open: in5, in6, en
  nor nor_1 (Zero, AluResult[0], AluResult[1], AluResult[2], AluResult[3], AluResult[4], AluResult[5], AluResult[6], AluResult[7], AluResult[9], AluResult[10], AluResult[11], AluResult[12], AluResult[13], AluResult[14], AluResult[15], AluResult[8]);

  // Notes on the sheet:
  //   Adder
  //   Substractor
  //   Move
endmodule

module RegBank (
  input  in_1,
  input  in_2,
  output out_3
);

  wire clock_1_out;

  Clock clock_1 (.out(clock_1_out));
  S_R_Flip_Flop s_r_ff_1 (.S(in_1), .R(in_2), .Q(out_3), .preset(clock_1_out));  // open: clk, Qn, reset, en
endmodule

module _1_bit_Register (
  input  Data,
  input  Load,
  input  clk,
  output Output
);

  wire and_1_out, and_2_out, not_1_out;

  and and_1 (and_1_out, Data, Load);
  not not_1 (not_1_out, Data);
  and and_2 (and_2_out, not_1_out, Load);
  S_R_Flip_Flop s_r_ff_1 (.S(and_1_out), .clk(clk), .R(and_2_out), .Q(Output));  // open: Qn, preset, reset, en
endmodule

module _16_bits_Register (
  input  [15:0] Data,
  input  load,
  input  clk,
  output [15:0] Dout
);

  _1_bit_Register u_1_bit_register_1 (.Data(Data[0]), .Output(Dout[0]), .Load(load), .clk(clk));
  _1_bit_Register u_1_bit_register_2 (.Data(Data[1]), .Output(Dout[1]), .Load(load), .clk(clk));
  _1_bit_Register u_1_bit_register_3 (.Data(Data[2]), .Output(Dout[2]), .Load(load), .clk(clk));
  _1_bit_Register u_1_bit_register_4 (.Data(Data[3]), .Output(Dout[3]), .Load(load), .clk(clk));
  _1_bit_Register u_1_bit_register_5 (.Data(Data[4]), .Output(Dout[4]), .Load(load), .clk(clk));
  _1_bit_Register u_1_bit_register_6 (.Data(Data[5]), .Output(Dout[5]), .Load(load), .clk(clk));
  _1_bit_Register u_1_bit_register_7 (.Data(Data[6]), .Output(Dout[6]), .Load(load), .clk(clk));
  _1_bit_Register u_1_bit_register_8 (.Data(Data[7]), .Output(Dout[7]), .Load(load), .clk(clk));
  _1_bit_Register u_1_bit_register_9 (.Data(Data[8]), .Output(Dout[8]), .Load(load), .clk(clk));
  _1_bit_Register u_1_bit_register_10 (.Data(Data[9]), .Output(Dout[9]), .Load(load), .clk(clk));
  _1_bit_Register u_1_bit_register_11 (.Data(Data[10]), .Output(Dout[10]), .Load(load), .clk(clk));
  _1_bit_Register u_1_bit_register_12 (.Data(Data[11]), .Output(Dout[11]), .Load(load), .clk(clk));
  _1_bit_Register u_1_bit_register_13 (.Data(Data[12]), .Output(Dout[12]), .Load(load), .clk(clk));
  _1_bit_Register u_1_bit_register_14 (.Data(Data[13]), .Output(Dout[13]), .Load(load), .clk(clk));
  _1_bit_Register u_1_bit_register_15 (.Data(Data[14]), .Output(Dout[14]), .Load(load), .clk(clk));
  _1_bit_Register u_1_bit_register_16 (.Data(Data[15]), .Output(Dout[15]), .Load(load), .clk(clk));
endmodule

// Reg bank
module Registerbank (
  input  [2:0] Reg_Select,
  input  Reg_load,
  input  [15:0] Data_In,
  input  clock,
  input  sp_increment,
  input  sp_decrement,
  output [15:0] DOUT1,
  output [15:0] DOUT2,
  output [15:0] DOUT3,
  output [15:0] DOUT4,
  output [15:0] DOUT5,
  output [15:0] DOUT6,
  output [15:0] DOUT7,
  output [15:0] DOUT8
);

  wire and_1_out, and_2_out, and_3_out, and_4_out, and_5_out, and_6_out, and_7_out, and_8_out,
       decoder_1_out0, decoder_1_out1, decoder_1_out2, decoder_1_out3, decoder_1_out4, decoder_1_out5,
       decoder_1_out6, decoder_1_out7;

  Decoder #(.select(3)) decoder_1 (
    .out0(decoder_1_out0), .out1(decoder_1_out1), .out2(decoder_1_out2), .out3(decoder_1_out3),
    .out4(decoder_1_out4), .out5(decoder_1_out5), .out6(decoder_1_out6), .out7(decoder_1_out7),
    .sel(Reg_Select));  // open: en
  and and_1 (and_1_out, decoder_1_out0, Reg_load);
  and and_2 (and_2_out, decoder_1_out1, Reg_load);
  and and_3 (and_3_out, decoder_1_out2, Reg_load);
  and and_4 (and_4_out, decoder_1_out3, Reg_load);
  and and_5 (and_5_out, decoder_1_out4, Reg_load);
  and and_6 (and_6_out, decoder_1_out5, Reg_load);
  and and_7 (and_7_out, decoder_1_out6, Reg_load);
  and and_8 (and_8_out, decoder_1_out7, Reg_load);
  reg7 reg7_1 (
    .din(Data_In), .clk(clock), .dout(DOUT8), .SP_plus_plus(sp_increment), .SP_minus_minus(sp_decrement),
    .LD(and_8_out));
  _16_bits_Register Register_0 (.Data(Data_In), .Dout(DOUT1), .load(and_1_out), .clk(clock));
  _16_bits_Register Register_1 (.Data(Data_In), .Dout(DOUT2), .load(and_2_out), .clk(clock));
  _16_bits_Register Register_2 (.Data(Data_In), .Dout(DOUT3), .load(and_3_out), .clk(clock));
  _16_bits_Register Register_3 (.Data(Data_In), .Dout(DOUT4), .load(and_4_out), .clk(clock));
  _16_bits_Register Register_4 (.Data(Data_In), .Dout(DOUT5), .load(and_5_out), .clk(clock));
  _16_bits_Register Register_5 (.Data(Data_In), .Dout(DOUT6), .load(and_6_out), .clk(clock));
  _16_bits_Register Register_6 (.Data(Data_In), .Dout(DOUT7), .load(and_7_out), .clk(clock));

  // Other names for the same wires on the sheet: sp_dec = sp_decrement; sp_inc = sp_increment
endmodule

module Instruction_Register (
  input  [11:0] in_1,
  input  load,
  input  clock,
  output [11:0] addr,
  output [2:0] dst,
  output [2:0] src1,
  output [2:0] src2,
  output [5:0] aluop
);

  _12_bits_Register u_12_bits_register_1 (.Data(in_1), .load(load), .clk(clock), .out_4(addr));

  assign aluop = addr[11:6];
  assign dst = addr[2:0];
  assign src1 = addr[8:6];
  assign src2 = addr[5:3];
endmodule

module PC (
  input  [11:0] input_data,
  input  pc_load,
  input  clock,
  input  increment,
  output [11:0] \output 
);

  wire or_1_out;
  wire [11:0] adder_1_out, multiplexer_1_out;

  or or_1 (or_1_out, pc_load, increment);
  _12_bits_Register u_12_bits_register_1 (.Data(multiplexer_1_out), .load(or_1_out), .clk(clock), .out_4(\output ));
  Adder #(.width(12)) adder_1 (.a(\output ), .b(12'h1), .out(adder_1_out));  // open: cin, cout
  Multiplexer #(.width(12), .enable("false")) multiplexer_1 (
    .in0(input_data), .in1(adder_1_out), .out(multiplexer_1_out), .sel(increment));
endmodule

module _12_bits_Register (
  input  [11:0] Data,
  input  load,
  input  clk,
  output [11:0] out_4
);

  _1_bit_Register u_1_bit_register_1 (.Data(Data[0]), .Output(out_4[0]), .Load(load), .clk(clk));
  _1_bit_Register u_1_bit_register_2 (.Data(Data[1]), .Output(out_4[1]), .Load(load), .clk(clk));
  _1_bit_Register u_1_bit_register_3 (.Data(Data[2]), .Output(out_4[2]), .Load(load), .clk(clk));
  _1_bit_Register u_1_bit_register_4 (.Data(Data[3]), .Output(out_4[3]), .Load(load), .clk(clk));
  _1_bit_Register u_1_bit_register_5 (.Data(Data[4]), .Output(out_4[4]), .Load(load), .clk(clk));
  _1_bit_Register u_1_bit_register_6 (.Data(Data[5]), .Output(out_4[5]), .Load(load), .clk(clk));
  _1_bit_Register u_1_bit_register_7 (.Data(Data[6]), .Output(out_4[6]), .Load(load), .clk(clk));
  _1_bit_Register u_1_bit_register_8 (.Data(Data[7]), .Output(out_4[7]), .Load(load), .clk(clk));
  _1_bit_Register u_1_bit_register_9 (.Data(Data[8]), .Output(out_4[8]), .Load(load), .clk(clk));
  _1_bit_Register u_1_bit_register_10 (.Data(Data[9]), .Output(out_4[9]), .Load(load), .clk(clk));
  _1_bit_Register u_1_bit_register_11 (.Data(Data[10]), .Output(out_4[10]), .Load(load), .clk(clk));
  _1_bit_Register u_1_bit_register_12 (.Data(Data[11]), .Output(out_4[11]), .Load(load), .clk(clk));
endmodule

module _4_bits_Register (
  input  [3:0] in_1,
  input  in_2,
  output [3:0] out_3
);

  _1_bit_Register u_1_bit_register_1 (.Data(in_1[0]), .Output(out_3[0]), .Load(1'b1), .clk(in_2));
  _1_bit_Register u_1_bit_register_2 (.Data(in_1[1]), .Output(out_3[1]), .Load(1'b1), .clk(in_2));
  _1_bit_Register u_1_bit_register_3 (.Data(in_1[2]), .Output(out_3[2]), .Load(1'b1), .clk(in_2));
  _1_bit_Register u_1_bit_register_4 (.Data(in_1[3]), .Output(out_3[3]), .Load(1'b1), .clk(in_2));
endmodule

module reg7 (
  input  clk,
  input  [15:0] din,
  input  LD,
  input  SP_plus_plus,
  input  SP_minus_minus,
  output [15:0] dout
);

  wire or_1_out, or_2_out;
  wire [3:0] data_0_3, data_4_7, data_8_11, data_12_15, multiplexer_1_out, multiplexer_2_out,
       multiplexer_3_out, multiplexer_4_out;
  wire [15:0] adder_1_out, subtractor_1_out;

  Multiplexer #(.width(4), .enable("false")) multiplexer_1 (
    .in0(din[3:0]), .in1(data_0_3), .out(multiplexer_1_out), .sel(or_1_out));
  Multiplexer #(.width(4), .enable("false")) multiplexer_2 (
    .in0(din[7:4]), .in1(data_4_7), .out(multiplexer_2_out), .sel(or_1_out));
  Multiplexer #(.width(4), .enable("false")) multiplexer_3 (
    .in0(din[11:8]), .in1(data_8_11), .out(multiplexer_3_out), .sel(or_1_out));
  Multiplexer #(.width(4), .enable("false")) multiplexer_4 (
    .in0(din[15:12]), .in1(data_12_15), .out(multiplexer_4_out), .sel(or_1_out));
  or or_1 (or_1_out, SP_plus_plus, SP_minus_minus);
  _4_bit_reg u_4_bit_reg_1 (.din(multiplexer_1_out), .clk(clk), .ld(or_2_out), .out_4(dout[3:0]));
  _4_bit_reg u_4_bit_reg_2 (.din(multiplexer_2_out), .clk(clk), .ld(or_2_out), .out_4(dout[7:4]));
  _4_bit_reg u_4_bit_reg_3 (.din(multiplexer_3_out), .clk(clk), .ld(or_2_out), .out_4(dout[11:8]));
  _4_bit_reg u_4_bit_reg_4 (.din(multiplexer_4_out), .clk(clk), .ld(or_2_out), .out_4(dout[15:12]));
  or or_2 (or_2_out, SP_plus_plus, SP_minus_minus, LD);
  Adder #(.width(16)) adder_1 (.a(dout), .b(16'h1), .out(adder_1_out));  // open: cin, cout
  Subtractor #(.width(16)) subtractor_1 (.a(dout), .b(16'h1), .out(subtractor_1_out));  // open: bin, bout
  Multiplexer #(.width(16), .enable("false")) multiplexer_5 (
    .in0(adder_1_out), .in1(subtractor_1_out), .out({data_12_15, data_8_11, data_4_7, data_0_3}),
    .sel(SP_minus_minus));
endmodule

module _1_bit_reg (
  input  clk,
  input  data_in,
  input  ld,
  output data_out
);

  wire and_1_out, and_2_out;

  and and_1 (and_1_out, data_in, ld);
  and and_2 (and_2_out, ~data_in, ld);  // AND_Gate
  S_R_Flip_Flop s_r_ff_1 (.S(and_1_out), .clk(clk), .R(and_2_out), .Q(data_out), .en(1'b1));  // open: Qn, preset, reset
endmodule

module Question2 (
  input  in_1,
  input  in_2,
  input  [15:0] input_device_1,
  input  [15:0] input_device_2
);

  wire and_1_out, and_2_out, and_3_out, and_4_out, button_1_out, button_2_out, clock, main_1_memld,
       not_1_out, not_2_out;
  wire [3:0] n16_bits_register_1_dout_2, n16_bits_register_1_dout_3;
  wire [7:0] n16_bits_register_1_dout;
  wire [10:0] main_1_addrout;
  wire [11:11] main_1_addrout_2;
  wire [15:0] main_1_dout, multiplexer_1_out, multiplexer_2_out, multiplexer_3_out, ram_1_data,
       switchboard_1_output, switchboard_2_output;

  and and_1 (and_1_out, main_1_addrout_2[11], main_1_addrout[10], ~main_1_addrout[9], ~main_1_addrout[8], main_1_addrout[7], main_1_addrout[6], main_1_addrout[5], main_1_addrout[4], main_1_addrout[3], main_1_addrout[2], main_1_addrout[1], ~1'b0);  // AND_Gate
  Button button_1 (.out(button_1_out));
  and and_2 (and_2_out, main_1_addrout_2[11], main_1_addrout[10], main_1_addrout[9], ~main_1_addrout[8], main_1_addrout[7], main_1_addrout[6], main_1_addrout[5], main_1_addrout[4], main_1_addrout[3], main_1_addrout[2], main_1_addrout[1], ~1'b0);  // AND_Gate
  SwitchBoard switchboard_1 (
    .switchboard(input_device_1), .enter(button_1_out), .A11(main_1_addrout_2[11]), .A0(main_1_addrout[0]),
    .clk(clock), .\output (switchboard_1_output));
  Button button_2 (.out(button_2_out));
  Multiplexer #(.width(16), .enable("false")) multiplexer_1 (
    .in0({16{1'b0}}), .in1(switchboard_1_output), .out(multiplexer_1_out), .sel(and_1_out));
  SwitchBoard switchboard_2 (
    .switchboard(input_device_2), .enter(button_2_out), .A11(main_1_addrout_2[11]), .A0(main_1_addrout[0]),
    .clk(clock), .\output (switchboard_2_output));
  Multiplexer #(.width(16), .enable("false")) multiplexer_2 (
    .in0(switchboard_1_output), .in1(switchboard_2_output), .out(multiplexer_2_out), .sel(and_2_out));
  main main_1 (
    .Dout(main_1_dout), .memld(main_1_memld), .clk(clock), .Datain(multiplexer_3_out),
    .Addrout({main_1_addrout_2[11], main_1_addrout}));
  RAM #(.addrWidth(11), .dataWidth(16), .bus("separate")) ram_1 (
    .addr(main_1_addrout), .din(main_1_dout), .data(ram_1_data), .str(and_3_out), .clk(clock));  // open: sel, ld, clr
  not not_1 (not_1_out, main_1_addrout_2[11]);
  Multiplexer #(.width(16), .enable("false")) multiplexer_3 (
    .in0(multiplexer_2_out), .in1(ram_1_data), .out(multiplexer_3_out), .sel(not_1_out));
  not not_2 (not_2_out, main_1_addrout_2[11]);
  and and_3 (and_3_out, not_2_out, main_1_memld);
  and and_4 (and_4_out, main_1_memld, main_1_addrout_2[11]);
  Hex_Digit_Display hex_digit_display_1 (.value(n16_bits_register_1_dout_3));  // open: dp
  _16_bits_Register u_16_bits_register_1 (
    .Data(main_1_dout),
    .Dout({n16_bits_register_1_dout_3, n16_bits_register_1_dout_2, n16_bits_register_1_dout}),
    .load(and_4_out), .clk(clock));
  Hex_Digit_Display hex_digit_display_2 (.value(n16_bits_register_1_dout_2));  // open: dp
  Hex_Digit_Display hex_digit_display_3 (.value(n16_bits_register_1_dout[7:4]));  // open: dp
  Hex_Digit_Display hex_digit_display_4 (.value(n16_bits_register_1_dout[3:0]));  // open: dp

  // Notes on the sheet:
  //   CFE
  //   EFE
  //   Memory
  //   Din
endmodule

module _4_bit_reg (
  input  clk,
  input  [3:0] din,
  input  ld,
  output [3:0] out_4
);

  _1_bit_reg u_1_bit_reg_1 (.data_in(din[0]), .clk(clk), .ld(ld), .data_out(out_4[0]));
  _1_bit_reg u_1_bit_reg_2 (.data_in(din[1]), .clk(clk), .ld(ld), .data_out(out_4[1]));
  _1_bit_reg u_1_bit_reg_3 (.data_in(din[2]), .clk(clk), .ld(ld), .data_out(out_4[2]));
  _1_bit_reg u_1_bit_reg_4 (.data_in(din[3]), .clk(clk), .ld(ld), .data_out(out_4[3]));
endmodule

module SwitchBoard (
  input  clk,
  input  [15:0] switchboard,
  input  A0,
  input  enter,
  input  A11,
  output [15:0] \output 
);

  wire and_1_out, and_2_out, not_1_out, s_r_ff_1_q;
  wire [15:0] bit_extender_1_out, n16_bits_register_1_dout;

  not not_1 (not_1_out, s_r_ff_1_q);
  _16_bits_Register u_16_bits_register_1 (
    .Data(switchboard), .Dout(n16_bits_register_1_dout), .load(and_1_out), .clk(clk));
  and and_1 (and_1_out, not_1_out, enter);
  and and_2 (and_2_out, A11, s_r_ff_1_q);
  S_R_Flip_Flop s_r_ff_1 (.S(and_1_out), .clk(clk), .R(and_2_out), .Q(s_r_ff_1_q));  // open: Qn, preset, reset, en
  assign bit_extender_1_out = {{15{1'b0}}, s_r_ff_1_q};  // Bit_Extender bit_extender_1
  Multiplexer #(.width(16), .enable("false")) multiplexer_1 (
    .in0(n16_bits_register_1_dout), .in1(bit_extender_1_out), .out(\output ), .sel(A0));
endmodule
