// Logisim project circ.circ as structural Verilog: 7 circuits, main circuit main
module main (
  input  in_1,
  input  in_2,
  input  in_3
);

  wire clock_1_out;
  wire [7:0] n8_bit_register_increment_decrement_1_out;

  Clock clock_1 (.out(clock_1_out));
  _8_bit_Register_Increment_Decrement u_8_bit_register_increment_decrement_1 (
    .LOAD(in_1), .CLK(clock_1_out), .INCREMENT(in_3), .DECREMENT(in_2),
    .OUT(n8_bit_register_increment_decrement_1_out));  // open: DATA
  Hex_Digit_Display hex_digit_display_1 (.value(n8_bit_register_increment_decrement_1_out[7:4]));  // open: dp
  // Probe on n8_bit_register_increment_decrement_1_out
  Hex_Digit_Display hex_digit_display_2 (.value(n8_bit_register_increment_decrement_1_out[3:0]));  // open: dp
endmodule

module Test (
  output LOAD,
  output DECREMENT,
  output INCREMENT
);

  wire clock_1_out;
  wire [7:0] n8_bit_register_increment_decrement_1_out, random_1_out;

  Clock clock_1 (.out(clock_1_out));
  Random random_1 (.clk(clock_1_out), .out(random_1_out));  // open: next, clr
  _8_bit_Register_Increment_Decrement u_8_bit_register_increment_decrement_1 (
    .LOAD(1'b1), .CLK(clock_1_out), .INCREMENT(1'b0), .DECREMENT(1'b0), .DATA(random_1_out),
    .OUT(n8_bit_register_increment_decrement_1_out));
  // Probe on n8_bit_register_increment_decrement_1_out
  Hex_Digit_Display hex_digit_display_1 (.value(n8_bit_register_increment_decrement_1_out[7:4]));  // open: dp
  Hex_Digit_Display hex_digit_display_2 (.value(n8_bit_register_increment_decrement_1_out[3:0]));  // open: dp

  assign DECREMENT = 1'b0;
  assign INCREMENT = 1'b0;
  assign LOAD = 1'b1;
endmodule

module _1_bit_Register (
  input  DATA,
  input  CLK,
  input  LOAD,
  output OUT
);

  wire and_1_out, and_2_out, not_1_out;

  not not_1 (not_1_out, DATA);
  and and_1 (and_1_out, DATA, LOAD);
  and and_2 (and_2_out, not_1_out, LOAD);
  S_R_Flip_Flop s_r_ff_1 (.S(and_1_out), .clk(CLK), .R(and_2_out), .Q(OUT));  // open: Qn, preset, reset, en
endmodule

module _2_bit_Register (
  input  CLK,
  input  [1:0] DATA,
  input  LOAD,
  output [1:0] OUT
);

  _1_bit_Register u_1_bit_register_1 (.DATA(DATA[0]), .CLK(CLK), .LOAD(LOAD), .OUT(OUT[0]));
  _1_bit_Register u_1_bit_register_2 (.DATA(DATA[1]), .CLK(CLK), .LOAD(LOAD), .OUT(OUT[1]));
endmodule

module _4_bit_Register (
  input  LOAD,
  input  [3:0] DATA,
  input  CLK,
  output [3:0] OUT
);

  _2_bit_Register u_2_bit_register_1 (.DATA(DATA[1:0]), .LOAD(LOAD), .CLK(CLK), .OUT(OUT[1:0]));
  _2_bit_Register u_2_bit_register_2 (.DATA(DATA[3:2]), .LOAD(LOAD), .CLK(CLK), .OUT(OUT[3:2]));
endmodule

module _8_bit_Register (
  input  LOAD,
  input  [7:0] DATA,
  input  CLK,
  output [7:0] OUT
);

  _4_bit_Register u_4_bit_register_1 (.LOAD(LOAD), .CLK(CLK), .OUT(OUT[3:0]), .DATA(DATA[3:0]));
  _4_bit_Register u_4_bit_register_2 (.LOAD(LOAD), .CLK(CLK), .OUT(OUT[7:4]), .DATA(DATA[7:4]));
endmodule

module _8_bit_Register_Increment_Decrement (
  input  LOAD,
  input  CLK,
  input  INCREMENT,
  input  DECREMENT,
  input  [7:0] DATA,
  output [7:0] OUT
);

  wire LOAD_N;
  wire [7:0] ADD_1, DATA_N, SUB_1;

  _8_bit_Register u_8_bit_register_1 (.LOAD(LOAD_N), .CLK(CLK), .DATA(DATA_N), .OUT(OUT));
  Adder adder_1 (.a(OUT), .b(8'h1), .out(ADD_1));  // open: cin, cout
  Subtractor subtractor_1 (.a(OUT), .b(8'h1), .out(SUB_1));  // open: bin, bout
  or or_1 (LOAD_N, INCREMENT, LOAD, DECREMENT);
  // Probe on {LOAD, DECREMENT, INCREMENT}
  Multiplexer #(.select(3), .width(8)) multiplexer_1 (
    .in0(OUT), .in1(ADD_1), .in2(SUB_1), .in3(OUT), .in4(DATA), .in5(OUT), .in6(OUT), .in7(OUT),
    .out(DATA_N), .sel({LOAD, DECREMENT, INCREMENT}), .en(1'b1));
  // Probe on DATA_N

  // Notes on the sheet:
  //   001 => INCREMENT 010 => DECREMENT 100=> LOAD
endmodule
