// Logisim project circ2.circ as structural Verilog: 2 circuits, main circuit main
module main (
  input  [7:0] in_1,
  input  LOAD,
  input  INC,
  input  DEC,
  output [7:0] OUTPUT
);

  BetterRegister betterregister_1 (.INPUT(in_1), .out_5(OUTPUT), .DECR(DEC), .INC(INC), .LOAD(LOAD));
  Hex_Digit_Display hex_digit_display_1 (.value(OUTPUT[7:4]));  // open: dp
  Hex_Digit_Display hex_digit_display_2 (.value(OUTPUT[3:0]));  // open: dp
endmodule

module BetterRegister (
  input  [7:0] INPUT,
  input  DECR,
  input  INC,
  input  LOAD,
  output [7:0] out_5
);

  wire and_1_out, and_2_out, and_3_out, and_4_out, and_5_out, and_6_out, and_7_out, and_8_out, and_9_out,
       and_10_out, and_11_out, and_12_out, and_13_out, and_14_out, and_15_out, and_16_out, CLK_out,
       not_1_out, not_2_out, not_3_out, not_4_out, not_5_out, not_6_out, not_7_out, not_8_out, or_1_out;
  wire [7:0] adder_1_out, multiplexer_1_out, subtractor_1_out;

  Adder adder_1 (.a(out_5), .b(8'h1), .out(adder_1_out));  // open: cin, cout
  Subtractor subtractor_1 (.a(out_5), .b(8'h1), .out(subtractor_1_out));  // open: bin, bout
  Multiplexer #(.select(2), .width(8), .enable("false")) multiplexer_1 (
    .in0(INPUT), .in1(adder_1_out), .in2(subtractor_1_out), .in3(subtractor_1_out), .out(multiplexer_1_out),
    .sel({DECR, INC}));
  or or_1 (or_1_out, DECR, INC, LOAD);
  and and_1 (and_1_out, multiplexer_1_out[0], or_1_out);
  not not_1 (not_1_out, multiplexer_1_out[0]);
  and and_2 (and_2_out, not_1_out, or_1_out);
  and and_3 (and_3_out, multiplexer_1_out[1], or_1_out);
  not not_2 (not_2_out, multiplexer_1_out[1]);
  and and_4 (and_4_out, not_2_out, or_1_out);
  and and_5 (and_5_out, multiplexer_1_out[2], or_1_out);
  not not_3 (not_3_out, multiplexer_1_out[2]);
  and and_6 (and_6_out, not_3_out, or_1_out);
  and and_7 (and_7_out, multiplexer_1_out[3], or_1_out);
  not not_4 (not_4_out, multiplexer_1_out[3]);
  and and_8 (and_8_out, not_4_out, or_1_out);
  and and_9 (and_9_out, multiplexer_1_out[4], or_1_out);
  not not_5 (not_5_out, multiplexer_1_out[4]);
  and and_10 (and_10_out, not_5_out, or_1_out);
  and and_11 (and_11_out, multiplexer_1_out[5], or_1_out);
  not not_6 (not_6_out, multiplexer_1_out[5]);
  and and_12 (and_12_out, not_6_out, or_1_out);
  and and_13 (and_13_out, multiplexer_1_out[6], or_1_out);
  not not_7 (not_7_out, multiplexer_1_out[6]);
  and and_14 (and_14_out, not_7_out, or_1_out);
  and and_15 (and_15_out, multiplexer_1_out[7], or_1_out);
  not not_8 (not_8_out, multiplexer_1_out[7]);
  and and_16 (and_16_out, not_8_out, or_1_out);
  Clock CLK (.out(CLK_out));
  S_R_Flip_Flop s_r_ff_1 (.S(and_1_out), .clk(CLK_out), .R(and_2_out), .Q(out_5[0]));  // open: Qn, preset, reset, en
  S_R_Flip_Flop s_r_ff_2 (.S(and_3_out), .clk(CLK_out), .R(and_4_out), .Q(out_5[1]));  // open: Qn, preset, reset, en
  S_R_Flip_Flop s_r_ff_3 (.S(and_5_out), .clk(CLK_out), .R(and_6_out), .Q(out_5[2]));  // open: Qn, preset, reset, en
  S_R_Flip_Flop s_r_ff_4 (.S(and_7_out), .clk(CLK_out), .R(and_8_out), .Q(out_5[3]));  // open: Qn, preset, reset, en
  S_R_Flip_Flop s_r_ff_5 (.S(and_9_out), .clk(CLK_out), .R(and_10_out), .Q(out_5[4]));  // open: Qn, preset, reset, en
  S_R_Flip_Flop s_r_ff_6 (.S(and_11_out), .clk(CLK_out), .R(and_12_out), .Q(out_5[5]));  // open: Qn, preset, reset, en
  S_R_Flip_Flop s_r_ff_7 (.S(and_13_out), .clk(CLK_out), .R(and_14_out), .Q(out_5[6]));  // open: Qn, preset, reset, en
  S_R_Flip_Flop s_r_ff_8 (.S(and_15_out), .clk(CLK_out), .R(and_16_out), .Q(out_5[7]));  // open: Qn, preset, reset, en
endmodule
