// Logisim project mammal.circ as structural Verilog: 21 circuits, main circuit Main
module Main (
  input  in_1,
  input  [15:0] INPUT_1,
  input  [15:0] INPUT_2
);

  wire and_1_out, and_2_out, BUTTON_1_out, BUTTON_2_out, CLOCK, comparator_1_eq, comparator_2_eq,
       comparator_3_eq, comparator_3_gt, comparator_3_lt, comparator_4_eq, comparator_5_eq, comparator_6_eq,
       comparator_7_eq, comparator_8_eq, comparator_9_eq, INT_ACK, MEMWT, n1_bit_register_1_out, or_1_out,
       pic_1_interrupt, timer_1_interrupt;
  wire [11:0] ADDR, multiplexer_1_out;
  wire [15:0] _7SEG_OUT, BUTTON_1, BUTTON_2, DIN, DOUT, INPUT_1_t, INPUT_2_t, INT_DEVICE_ID,
       multiplexer_2_out, multiplexer_3_out, multiplexer_4_out, multiplexer_5_out, multiplexer_6_out,
       multiplexer_7_out, ram_1_data, SWITCH, TIME;

  Clock clock_1 (.out(CLOCK));
  CPU cpu_1 (
    .INT(pic_1_interrupt), .MEMLOAD(MEMWT), .ADDRBUS(ADDR), .DATA_OUT(DOUT), .DATA_IN(DIN), .INTACK(INT_ACK),
    .CLOCK(CLOCK));
  PIC pic_1 (
    .DEVICE_0(timer_1_interrupt), .DEVICE_ID(INT_DEVICE_ID), .INTERRUPT(pic_1_interrupt), .CLOCK(CLOCK),
    .INT_ACK(INT_ACK));  // open: DEVICE_1, DEVICE_2, DEVICE_3, DEVICE_4, DEVICE_5, DEVICE_6, DEVICE_7
  Timer timer_1 (.INTERRUPT(timer_1_interrupt), .CLOCK(CLOCK), .TIME(TIME));
  assign SWITCH = {{15{1'b0}}, in_1};  // Bit_Extender bit_extender_1
  Button_part u_BUTTON_1 (.out(BUTTON_1_out));
  Comparator #(.width(12)) comparator_1 (.a(12'ha08), .b(ADDR), .eq(comparator_1_eq));  // open: gt, lt
  Button u_button_1_dup2 (.CLOCK(CLOCK), .IN(BUTTON_1_out), .OUT(BUTTON_1), .RESET(comparator_1_eq));
  // Probe on BUTTON_1
  Button_part u_BUTTON_2 (.out(BUTTON_2_out));
  Button u_button_2_dup2 (.CLOCK(CLOCK), .IN(BUTTON_2_out), .OUT(BUTTON_2), .RESET(comparator_2_eq));
  Comparator #(.width(12)) comparator_2 (.a(12'ha06), .b(ADDR), .eq(comparator_2_eq));  // open: gt, lt
  Comparator #(.width(12)) comparator_3 (
    .a(12'ha10), .b(ADDR), .gt(comparator_3_gt), .eq(comparator_3_eq), .lt(comparator_3_lt));
  Multiplexer #(.width(12), .enable("false")) multiplexer_1 (
    .in0({12{1'b0}}), .in1(ADDR), .out(multiplexer_1_out), .sel(n1_bit_register_1_out));
  // Probe on ADDR
  _1_bit_Register u_1_bit_register_1 (.DATA(1'b1), .CLK(CLOCK), .LOAD(1'b1), .OUT(n1_bit_register_1_out));
  _16_bit_Register_S u_16_bit_register_s_1 (.LOAD(and_1_out), .CLK(CLOCK), .DATA(DOUT), .OUT(_7SEG_OUT));
  and and_1 (and_1_out, comparator_3_eq, MEMWT);
  and and_2 (and_2_out, MEMWT, or_1_out);
  or or_1 (or_1_out, comparator_3_gt, comparator_3_lt);
  _16_bit_Register_S u_16_bit_register_s_2 (.LOAD(1'b1), .CLK(CLOCK), .DATA(INPUT_1), .OUT(INPUT_1_t));
  RAM #(.addrWidth(12), .dataWidth(16), .bus("separate")) ram_1 (
    .addr(multiplexer_1_out), .din(DOUT), .data(ram_1_data), .str(and_2_out), .clk(CLOCK));  // open: sel, ld, clr
  _16_bit_Register_S u_16_bit_register_s_3 (.LOAD(1'b1), .CLK(CLOCK), .DATA(INPUT_2), .OUT(INPUT_2_t));
  Comparator #(.width(12)) comparator_4 (.a(12'ha00), .b(ADDR), .eq(comparator_4_eq));  // open: gt, lt
  Comparator #(.width(12)) comparator_5 (.a(12'ha02), .b(ADDR), .eq(comparator_5_eq));  // open: gt, lt
  Comparator #(.width(12)) comparator_6 (.a(12'ha04), .b(ADDR), .eq(comparator_6_eq));  // open: gt, lt
  Comparator #(.width(12)) comparator_7 (.a(12'ha06), .b(ADDR), .eq(comparator_7_eq));  // open: gt, lt
  Comparator #(.width(12)) comparator_8 (.a(12'ha08), .b(ADDR), .eq(comparator_8_eq));  // open: gt, lt
  Comparator #(.width(12)) comparator_9 (.a(12'ha12), .b(ADDR), .eq(comparator_9_eq));  // open: gt, lt
  Multiplexer #(.width(16), .enable("false")) multiplexer_2 (
    .in0(ram_1_data), .in1(TIME), .out(multiplexer_2_out), .sel(comparator_4_eq));
  Multiplexer #(.width(16), .enable("false")) multiplexer_3 (
    .in0(multiplexer_2_out), .in1(INPUT_2_t), .out(multiplexer_3_out), .sel(comparator_5_eq));
  Multiplexer #(.width(16), .enable("false")) multiplexer_4 (
    .in0(multiplexer_3_out), .in1(INPUT_1_t), .out(multiplexer_4_out), .sel(comparator_6_eq));
  Multiplexer #(.width(16), .enable("false")) multiplexer_5 (
    .in0(multiplexer_4_out), .in1(BUTTON_2), .out(multiplexer_5_out), .sel(comparator_7_eq));
  Multiplexer #(.width(16), .enable("false")) multiplexer_6 (
    .in0(multiplexer_5_out), .in1(BUTTON_1), .out(multiplexer_6_out), .sel(comparator_8_eq));
  Multiplexer #(.width(16), .enable("false")) multiplexer_7 (
    .in0(multiplexer_6_out), .in1(SWITCH), .out(multiplexer_7_out), .sel(comparator_9_eq));
  Multiplexer #(.width(16), .enable("false")) multiplexer_8 (
    .in0(multiplexer_7_out), .in1(INT_DEVICE_ID), .out(DIN), .sel(INT_ACK));
  // Probe on DIN
  Hex_Digit_Display hex_digit_display_1 (.value(_7SEG_OUT[15:12]));  // open: dp
  Hex_Digit_Display hex_digit_display_2 (.value(_7SEG_OUT[11:8]));  // open: dp
  Hex_Digit_Display hex_digit_display_3 (.value(_7SEG_OUT[7:4]));  // open: dp
  Hex_Digit_Display hex_digit_display_4 (.value(_7SEG_OUT[3:0]));  // open: dp
endmodule

module CPU (
  input  INT,
  input  [15:0] DATA_IN,
  input  CLOCK,
  output INTACK,
  output MEMLOAD,
  output [11:0] ADDRBUS,
  output [15:0] DATA_OUT
);

  wire ALU_zero_flag, control_unit_1_intld, control_unit_1_irld, control_unit_1_mux, control_unit_1_pcinc,
       control_unit_1_pcld, control_unit_1_pcmux, control_unit_1_regld, control_unit_1_sp_minus_minus,
       control_unit_1_sp_plus_plus, control_unit_1_zfld, control_unit_1_zfpop, zf_unit_1_zf;
  wire [1:0] control_unit_1_armux, control_unit_1_datamux;
  wire [2:0] IR_out_2, IR_out_3, IR_out_4;
  wire [5:3] IR_out;
  wire [11:0] adder_1_out, adder_2_out, INT_REG_out, multiplexer_2_out, PC_out;
  wire [15:0] ALU_result, multiplexer_4_out, multiplexer_5_out, multiplexer_6_out, regbank_1_reg0,
       regbank_1_reg1, regbank_1_reg2, regbank_1_reg3, regbank_1_reg4, regbank_1_reg5, regbank_1_reg6,
       regbank_1_reg7, Zero_Extender_extended_value, zf_unit_1_mem_out;

  Control_Unit control_unit_1 (
    .ZF(zf_unit_1_zf), .OPCode(DATA_IN[15:12]), .Clock(CLOCK), .INT(INT), .DATAMUX(control_unit_1_datamux),
    .PCMUX(control_unit_1_pcmux), .SP_plus_plus(control_unit_1_sp_plus_plus),
    .SP_minus_minus(control_unit_1_sp_minus_minus), .PCLD(control_unit_1_pcld), .PCINC(control_unit_1_pcinc),
    .ARMUX(control_unit_1_armux), .REGLD(control_unit_1_regld), .ZFLD(control_unit_1_zfld),
    .MUX(control_unit_1_mux), .MEMLD(MEMLOAD), .IRLD(control_unit_1_irld), .INTLD(control_unit_1_intld),
    .ZFPOP(control_unit_1_zfpop), .INTACK(INTACK));
  // Probe on control_unit_1_armux
  Adder #(.width(12)) adder_1 (
    .a(PC_out), .b({IR_out, IR_out_3, IR_out_4, IR_out_2}), .out(adder_1_out));  // open: cin, cout
  // Probe on INT_REG_out
  // Probe on adder_2_out
  Multiplexer #(.select(2), .width(12), .enable("false")) multiplexer_1 (
    .in0(PC_out), .in1(multiplexer_6_out[11:0]), .in2(regbank_1_reg7[11:0]), .in3(INT_REG_out),
    .out(ADDRBUS), .sel(control_unit_1_armux));
  Program_Counter PC (
    .LOAD(control_unit_1_pcld), .CLK(CLOCK), .DATA(multiplexer_2_out), .OUT(PC_out),
    .PCINC(control_unit_1_pcinc));
  Multiplexer #(.width(12), .enable("false")) multiplexer_2 (
    .in0(adder_1_out), .in1(DATA_IN[11:0]), .out(multiplexer_2_out), .sel(control_unit_1_pcmux));
  Interrupt_Register INT_REG (.LOAD(control_unit_1_intld), .CLK(CLOCK), .DATA(adder_2_out), .OUT(INT_REG_out));
  Adder #(.width(12)) adder_2 (.a(12'h7f0), .b({{9{1'b0}}, DATA_IN[2:0]}), .out(adder_2_out));  // open: cin, cout
  // Probe on ADDRBUS
  _12to16_Extender Zero_Extender (.Extended_Value(Zero_Extender_extended_value), .Input(PC_out));
  // Probe on DATA_IN
  // Probe on {{9{1'b0}}, DATA_IN[2:0]}
  // Probe on IR_out_2
  RegBank regbank_1 (
    .WriteReg(IR_out_2), .Data(multiplexer_5_out), .Clock(CLOCK),
    .Sp_minus_minus(control_unit_1_sp_minus_minus), .RegLD(control_unit_1_regld),
    .Sp_plus_plus(control_unit_1_sp_plus_plus), .reg0(regbank_1_reg0), .reg4(regbank_1_reg4),
    .reg1(regbank_1_reg1), .reg2(regbank_1_reg2), .reg3(regbank_1_reg3), .reg5(regbank_1_reg5),
    .reg6(regbank_1_reg6), .reg7(regbank_1_reg7));
  Multiplexer #(.select(2), .width(16), .enable("false")) multiplexer_3 (
    .in0(multiplexer_4_out), .in1(Zero_Extender_extended_value), .in2(zf_unit_1_mem_out), .out(DATA_OUT),
    .sel(control_unit_1_datamux));  // open: in3
  ZF_Unit zf_unit_1 (
    .D_0(DATA_IN[0]), .ZF_POP(control_unit_1_zfpop), .CLOCK(CLOCK), .ZF_LD(control_unit_1_zfld),
    .ZF_IN(ALU_zero_flag), .ZF(zf_unit_1_zf), .MEM_OUT(zf_unit_1_mem_out));
  Multiplexer #(.select(3), .width(16)) multiplexer_4 (
    .in0(regbank_1_reg0), .in1(regbank_1_reg1), .in2(regbank_1_reg2), .in3(regbank_1_reg3),
    .in4(regbank_1_reg4), .in5(regbank_1_reg5), .in6(regbank_1_reg6), .in7(regbank_1_reg7),
    .out(multiplexer_4_out), .sel(IR_out_3));  // open: en
  // Probe on multiplexer_4_out
  Multiplexer #(.width(16), .enable("false")) multiplexer_5 (
    .in0(ALU_result), .in1(DATA_IN), .out(multiplexer_5_out), .sel(control_unit_1_mux));
  // Probe on DATA_IN[15:12]
  Multiplexer #(.select(3), .width(16)) multiplexer_6 (
    .in0(regbank_1_reg0), .in1(regbank_1_reg1), .in2(regbank_1_reg2), .in3(regbank_1_reg3),
    .in4(regbank_1_reg4), .in5(regbank_1_reg5), .in6(regbank_1_reg6), .in7(regbank_1_reg7),
    .out(multiplexer_6_out), .sel(IR_out_4));  // open: en
  ALU ALU (
    .r1(multiplexer_4_out), .r2(multiplexer_6_out), .result(ALU_result), .ALU_Operation({IR_out, IR_out_3}),
    .zero_flag(ALU_zero_flag));
  // Probe on {IR_out, IR_out_3}
  // Probe on multiplexer_6_out
  Instruction_Register IR (
    .LOAD(control_unit_1_irld), .CLK(CLOCK), .DATA(DATA_IN[11:0]),
    .OUT({IR_out, IR_out_3, IR_out_4, IR_out_2}));
  // Probe on DATA_IN[11:0]
endmodule

module PIC (
  input  DEVICE_0,
  input  DEVICE_1,
  input  DEVICE_2,
  input  DEVICE_3,
  input  DEVICE_4,
  input  DEVICE_5,
  input  DEVICE_6,
  input  DEVICE_7,
  input  INT_ACK,
  input  CLOCK,
  output [15:0] DEVICE_ID,
  output INTERRUPT
);

  wire priority_encoder_1_gs;
  wire [2:0] priority_encoder_1_out;
  wire [15:0] bit_extender_1_out;

  Priority_Encoder #(.disabled(0)) priority_encoder_1 (
    .in0(DEVICE_0), .in1(DEVICE_1), .in2(DEVICE_2), .in3(DEVICE_3), .in4(DEVICE_4), .in5(DEVICE_5),
    .in6(DEVICE_6), .in7(DEVICE_7), .out(priority_encoder_1_out), .gs(priority_encoder_1_gs));  // open: en_in, en_out
  assign bit_extender_1_out = {{13{1'b0}}, priority_encoder_1_out};  // Bit_Extender bit_extender_1
  S_R_Flip_Flop s_r_ff_1 (
    .S(priority_encoder_1_gs), .clk(CLOCK), .R(INT_ACK), .Q(INTERRUPT));  // open: Qn, preset, reset, en
  _16_bit_Register_S u_16_bit_register_s_1 (.LOAD(1'b1), .CLK(CLOCK), .DATA(bit_extender_1_out), .OUT(DEVICE_ID));
endmodule

module ALU (
  input  [15:0] r1,
  input  [15:0] r2,
  input  [5:0] ALU_Operation,
  output [15:0] result,
  output zero_flag
);

  wire and_2_out, OR_2_out;
  wire [15:0] adder_1_out, adder_2_out, AND_out, multiplexer_1_out, multiplexer_2_out, not_1_out, OR_out,
       subtractor_1_out, subtractor_2_out, XOR_out;

  // Probe on r1
  // Probe on r2
  assign AND_out = r2 & r1;  // AND_Gate AND, 16 bits wide
  assign OR_out = r2 | r1;  // OR_Gate OR, 16 bits wide
  assign XOR_out = r1 ^ r2;  // XOR_Gate XOR, 16 bits wide
  assign not_1_out = ~r2;  // NOT_Gate not_1, 16 bits wide
  Adder #(.width(16)) adder_1 (.a(r2), .b(16'h1), .out(adder_1_out), .cin(1'b0));  // open: cout
  Subtractor #(.width(16)) subtractor_1 (.a(r2), .b(16'h1), .out(subtractor_1_out), .bin(1'b0));  // open: bout
  Adder #(.width(16)) adder_2 (.a(r1), .b(r2), .out(adder_2_out), .cin(1'b0));  // open: cout
  Subtractor #(.width(16)) subtractor_2 (.a(r1), .b(r2), .out(subtractor_2_out), .bin(1'b0));  // open: bout
  Multiplexer #(.select(3), .width(16), .disabled(0), .enable("false")) multiplexer_1 (
    .in0(adder_2_out), .in1(subtractor_2_out), .in2(AND_out), .in3(OR_out), .in4(XOR_out),
    .out(multiplexer_1_out), .sel(ALU_Operation[5:3]));  // open: in5, in6, in7
  Multiplexer #(.select(3), .width(16), .disabled(0), .enable("false")) multiplexer_2 (
    .in0(not_1_out), .in1(r2), .in2(adder_1_out), .in3(subtractor_1_out), .out(multiplexer_2_out),
    .sel(ALU_Operation[2:0]));  // open: in4, in5, in6, in7
  Multiplexer #(.width(16), .enable("false")) multiplexer_3 (
    .in0(multiplexer_1_out), .in1(multiplexer_2_out), .out(result), .sel(and_2_out));
  and and_2 (and_2_out, ALU_Operation[3], ALU_Operation[4], ALU_Operation[5]);
  // Probe on result
  or OR_2 (OR_2_out, result[15], result[14], result[13], result[12], result[11], result[10], result[9], result[8], result[7], result[6], result[5], result[4], result[3], result[2], result[1], result[0]);
  not not_2 (zero_flag, OR_2_out);
endmodule

module Timer (
  input  CLOCK,
  output INTERRUPT,
  output [15:0] TIME
);

  wire [15:0] adder_1_out, adder_2_out, multiplexer_1_out, n16_bit_register_s_1_out;

  _16_bit_Register_S u_16_bit_register_s_1 (
    .LOAD(1'b1), .CLK(CLOCK), .DATA(multiplexer_1_out),
    .OUT({n16_bit_register_s_1_out[15:9], INTERRUPT, n16_bit_register_s_1_out[7:0]}));
  Multiplexer #(.width(16), .enable("false")) multiplexer_1 (
    .in0(adder_1_out), .in1({16{1'b0}}), .out(multiplexer_1_out), .sel(INTERRUPT));
  Adder #(.width(16)) adder_1 (
    .a(16'h1), .b({n16_bit_register_s_1_out[15:9], INTERRUPT, n16_bit_register_s_1_out[7:0]}),
    .out(adder_1_out));  // open: cin, cout
  _16_bit_Register_S u_16_bit_register_s_2 (.LOAD(INTERRUPT), .CLK(CLOCK), .DATA(adder_2_out), .OUT(TIME));
  Adder #(.width(16)) adder_2 (.a(16'h1), .b(TIME), .out(adder_2_out));  // open: cin, cout
endmodule

module Button (
  input  CLOCK,
  input  IN,
  input  RESET,
  output [15:0] OUT
);

  wire and_1_out, and_2_out, and_3_out, not_1_out, not_2_out, s_r_ff_1_q, s_r_ff_2_q, s_r_ff_3_q;

  not not_1 (not_1_out, IN);
  S_R_Flip_Flop s_r_ff_1 (.S(IN), .clk(CLOCK), .R(not_1_out), .Q(s_r_ff_1_q));  // open: Qn, preset, reset, en
  S_R_Flip_Flop s_r_ff_2 (.S(s_r_ff_1_q), .clk(CLOCK), .R(not_2_out), .Q(s_r_ff_2_q));  // open: Qn, preset, reset, en
  not not_2 (not_2_out, s_r_ff_1_q);
  and and_1 (and_1_out, s_r_ff_1_q, ~s_r_ff_2_q);  // AND_Gate
  and and_2 (and_2_out, ~s_r_ff_3_q, and_1_out);  // AND_Gate
  and and_3 (and_3_out, RESET, s_r_ff_3_q);
  S_R_Flip_Flop s_r_ff_3 (.S(and_2_out), .clk(CLOCK), .R(and_3_out), .Q(s_r_ff_3_q));  // open: Qn, preset, reset, en
  assign OUT = {{15{1'b0}}, s_r_ff_3_q};  // Bit_Extender bit_extender_1
endmodule

module Control_Unit (
  input  [3:0] OPCode,
  input  ZF,
  input  INT,
  input  Clock,
  output PCMUX,
  output SP_plus_plus,
  output SP_minus_minus,
  output PCLD,
  output PCINC,
  output REGLD,
  output ZFLD,
  output MUX,
  output MEMLD,
  output IRLD,
  output INTLD,
  output ZFPOP,
  output INTACK,
  output [1:0] DATAMUX,
  output [1:0] ARMUX
);

  wire and_2_out, and_3_out, IFRST, IFSET, INT_ACCEPT_q;
  wire [1:1] and_1_out;
  wire [3:0] multiplexer_1_out;
  wire [4:0] multiplexer_2_out, multiplexer_3_out, n5_bit_register_1_out, NEXT_STATE;
  wire [24:24] rom_1_data;

  and and_1 (and_1_out[1], ~OPCode[0], ~OPCode[1], OPCode[2], ~OPCode[3]);  // AND_Gate
  // Probe on {and_1_out[1], ZF}
  Multiplexer #(.select(2), .width(4)) multiplexer_1 (
    .in0(OPCode), .in1(OPCode), .in2(4'b0000), .in3(4'b0101), .out(multiplexer_1_out),
    .sel({and_1_out[1], ZF}));  // open: en
  Multiplexer #(.width(5)) multiplexer_2 (
    .in0(NEXT_STATE), .in1({1'b0, multiplexer_1_out}), .out(multiplexer_2_out), .sel(rom_1_data[24]));  // open: en
  Multiplexer #(.width(5)) multiplexer_3 (
    .in0(multiplexer_2_out), .in1(5'b10011), .out(multiplexer_3_out), .sel(and_2_out));  // open: en
  _5_bit_Register u_5_bit_register_1 (.LOAD(1'b1), .CLK(Clock), .OUT(n5_bit_register_1_out), .DATA(multiplexer_3_out));
  ROM #(.addrWidth(5), .dataWidth(25)) rom_1 (
    .addr(n5_bit_register_1_out),
    .data({rom_1_data[24], DATAMUX, PCMUX, SP_plus_plus, SP_minus_minus, PCLD, PCINC, ARMUX, REGLD, ZFLD, MUX, MEMLD, IRLD, INTLD, ZFPOP, IFSET, IFRST, INTACK, NEXT_STATE}));  // open: sel
  and and_2 (and_2_out, INT, INT_ACCEPT_q, and_3_out);
  and and_3 (and_3_out, ~NEXT_STATE[4], ~NEXT_STATE[3], ~NEXT_STATE[2], ~NEXT_STATE[1], ~NEXT_STATE[0]);  // AND_Gate
  S_R_Flip_Flop INT_ACCEPT (.S(IFSET), .clk(Clock), .R(IFRST), .Q(INT_ACCEPT_q));  // open: Qn, preset, reset, en

  // Notes on the sheet:
  //   contents of rom_1 (hex, n*v repeats v):
  //   102041f 25000 d000 8800 0 40000 0 6000 90000 100011 550800 100012 80 40 10000f 111110 250000 15000
  //   251000 490854 890a35 258000
  //   Fetch
  //   ISR (address of INT1)
endmodule

module ZF_Unit (
  input  D_0,
  input  ZF_POP,
  input  CLOCK,
  input  ZF_LD,
  input  ZF_IN,
  output [15:0] MEM_OUT,
  output ZF
);

  wire and_1_out, and_2_out, and_3_out, and_4_out, or_1_out, or_2_out;

  and and_1 (and_1_out, D_0, ZF_POP);
  and and_2 (and_2_out, ZF_POP, ~D_0);  // AND_Gate
  and and_3 (and_3_out, ZF_LD, ZF_IN);
  and and_4 (and_4_out, ~ZF_IN, ZF_LD);  // AND_Gate
  or or_1 (or_1_out, and_1_out, and_3_out);
  or or_2 (or_2_out, and_2_out, and_4_out);
  S_R_Flip_Flop s_r_ff_1 (.S(or_1_out), .clk(CLOCK), .R(or_2_out), .Q(MEM_OUT[0]));  // open: Qn, preset, reset, en

  assign MEM_OUT[15:1] = {15{1'b0}};
  assign ZF = MEM_OUT[0];
endmodule

module _1_bit_Register (
  input  DATA,
  input  CLK,
  input  LOAD,
  output OUT
);

  wire and_1_out, and_2_out, not_1_out;

  not not_1 (not_1_out, DATA);
  and and_1 (and_1_out, DATA, LOAD);
  and and_2 (and_2_out, not_1_out, LOAD);
  S_R_Flip_Flop s_r_ff_1 (.S(and_1_out), .clk(CLK), .R(and_2_out), .Q(OUT));  // open: Qn, preset, reset, en
endmodule

module _2_bit_Register (
  input  CLK,
  input  [1:0] DATA,
  input  LOAD,
  output [1:0] OUT
);

  _1_bit_Register u_1_bit_register_1 (.DATA(DATA[0]), .CLK(CLK), .LOAD(LOAD), .OUT(OUT[0]));
  _1_bit_Register u_1_bit_register_2 (.DATA(DATA[1]), .CLK(CLK), .LOAD(LOAD), .OUT(OUT[1]));
endmodule

module _4_bit_Register (
  input  LOAD,
  input  [3:0] DATA,
  input  CLK,
  output [3:0] OUT
);

  _2_bit_Register u_2_bit_register_1 (.DATA(DATA[1:0]), .LOAD(LOAD), .CLK(CLK), .OUT(OUT[1:0]));
  _2_bit_Register u_2_bit_register_2 (.DATA(DATA[3:2]), .LOAD(LOAD), .CLK(CLK), .OUT(OUT[3:2]));
endmodule

module _5_bit_Register (
  input  LOAD,
  input  [4:0] DATA,
  input  CLK,
  output [4:0] OUT
);

  _2_bit_Register u_2_bit_register_1 (.DATA(DATA[1:0]), .LOAD(LOAD), .CLK(CLK), .OUT(OUT[1:0]));
  _2_bit_Register u_2_bit_register_2 (.DATA(DATA[3:2]), .LOAD(LOAD), .CLK(CLK), .OUT(OUT[3:2]));
  _1_bit_Register u_1_bit_register_1 (.DATA(DATA[4]), .CLK(CLK), .LOAD(LOAD), .OUT(OUT[4]));
endmodule

module _8_bit_Register (
  input  LOAD,
  input  [7:0] DATA,
  input  CLK,
  output [7:0] OUT
);

  _4_bit_Register u_4_bit_register_1 (.LOAD(LOAD), .CLK(CLK), .OUT(OUT[3:0]), .DATA(DATA[3:0]));
  _4_bit_Register u_4_bit_register_2 (.LOAD(LOAD), .CLK(CLK), .OUT(OUT[7:4]), .DATA(DATA[7:4]));
endmodule

module _12_bit_Register (
  input  [11:0] DATA,
  input  LOAD,
  input  CLOCK,
  output [11:0] OUT
);

  _2_bit_Register u_2_bit_register_1 (.DATA(DATA[11:10]), .LOAD(LOAD), .CLK(CLOCK), .OUT(OUT[11:10]));
  _2_bit_Register u_2_bit_register_2 (.DATA(DATA[9:8]), .LOAD(LOAD), .CLK(CLOCK), .OUT(OUT[9:8]));
  _2_bit_Register u_2_bit_register_3 (.DATA(DATA[7:6]), .LOAD(LOAD), .CLK(CLOCK), .OUT(OUT[7:6]));
  _2_bit_Register u_2_bit_register_4 (.DATA(DATA[3:2]), .LOAD(LOAD), .CLK(CLOCK), .OUT(OUT[3:2]));
  _2_bit_Register u_2_bit_register_5 (.DATA(DATA[5:4]), .LOAD(LOAD), .CLK(CLOCK), .OUT(OUT[5:4]));
  _2_bit_Register u_2_bit_register_6 (.DATA(DATA[1:0]), .LOAD(LOAD), .CLK(CLOCK), .OUT(OUT[1:0]));
endmodule

module _16_bit_Register (
  input  LOAD,
  input  [15:0] DATA,
  input  CLK,
  output [15:0] OUT
);

  _8_bit_Register u_8_bit_register_1 (.LOAD(LOAD), .CLK(CLK), .DATA(DATA[15:8]), .OUT(OUT[15:8]));
  _8_bit_Register u_8_bit_register_2 (.LOAD(LOAD), .CLK(CLK), .DATA(DATA[7:0]), .OUT(OUT[7:0]));
endmodule

// REG-16
module _16_bit_Register_S (
  input  LOAD,
  input  [15:0] DATA,
  input  CLK,
  output [15:0] OUT
);

  _8_bit_Register u_8_bit_register_1 (.LOAD(LOAD), .CLK(CLK), .DATA(DATA[15:8]), .OUT(OUT[15:8]));
  _8_bit_Register u_8_bit_register_2 (.LOAD(LOAD), .CLK(CLK), .DATA(DATA[7:0]), .OUT(OUT[7:0]));
endmodule

module Program_Counter (
  input  [11:0] DATA,
  input  CLK,
  input  LOAD,
  input  PCINC,
  output [11:0] OUT
);

  wire or_1_out;
  wire [11:0] adder_1_out, multiplexer_1_out;

  _12_bit_Register u_12_bit_register_1 (.LOAD(or_1_out), .CLOCK(CLK), .DATA(multiplexer_1_out), .OUT(OUT));
  or or_1 (or_1_out, LOAD, PCINC);
  Multiplexer #(.select(2), .width(12), .enable("false")) multiplexer_1 (
    .in0(OUT), .in1(adder_1_out), .in2(DATA), .in3(OUT), .out(multiplexer_1_out), .sel({LOAD, PCINC}));
  Adder #(.width(12)) adder_1 (.a(12'h1), .b(OUT), .out(adder_1_out));  // open: cin, cout
endmodule

module Instruction_Register (
  input  [11:0] DATA,
  input  CLK,
  input  LOAD,
  output [11:0] OUT
);

  _12_bit_Register u_12_bit_register_1 (.LOAD(LOAD), .CLOCK(CLK), .DATA(DATA), .OUT(OUT));
endmodule

module Interrupt_Register (
  input  LOAD,
  input  [11:0] DATA,
  input  CLK,
  output [11:0] OUT
);

  _4_bit_Register u_4_bit_register_1 (.LOAD(LOAD), .CLK(CLK), .OUT(OUT[3:0]), .DATA(DATA[3:0]));
  _4_bit_Register u_4_bit_register_2 (.LOAD(LOAD), .CLK(CLK), .OUT(OUT[7:4]), .DATA(DATA[7:4]));
  _4_bit_Register u_4_bit_register_3 (.LOAD(LOAD), .CLK(CLK), .OUT(OUT[11:8]), .DATA(DATA[11:8]));
endmodule

// REG BANK
module RegBank (
  input  [2:0] WriteReg,
  input  [15:0] Data,
  input  Sp_minus_minus,
  input  Sp_plus_plus,
  input  Clock,
  input  RegLD,
  output [15:0] reg6,
  output [15:0] reg4,
  output [15:0] reg5,
  output [15:0] reg0,
  output [15:0] reg1,
  output [15:0] reg2,
  output [15:0] reg3,
  output [15:0] reg7
);

  wire and_1_out, and_2_out, and_3_out, and_4_out, and_5_out, and_6_out, and_7_out, and_8_out,
       decoder_1_out0, decoder_1_out1, decoder_1_out2, decoder_1_out3, decoder_1_out4, decoder_1_out5,
       decoder_1_out6, decoder_1_out7;
  wire [15:0] adder_1_out, multiplexer_1_out, subtractor_1_out;

  Decoder #(.select(3)) decoder_1 (
    .out0(decoder_1_out0), .out1(decoder_1_out1), .out2(decoder_1_out2), .out3(decoder_1_out3),
    .out4(decoder_1_out4), .out5(decoder_1_out5), .out6(decoder_1_out6), .out7(decoder_1_out7), .sel(WriteReg));  // open: en
  and and_1 (and_1_out, decoder_1_out0, RegLD);
  and and_2 (and_2_out, decoder_1_out4, RegLD);
  _16_bit_Register r0 (.LOAD(and_1_out), .CLK(Clock), .DATA(Data), .OUT(reg0));
  _16_bit_Register r4 (.LOAD(and_2_out), .CLK(Clock), .DATA(Data), .OUT(reg4));
  and and_3 (and_3_out, decoder_1_out1, RegLD);
  // Probe on reg4
  and and_4 (and_4_out, decoder_1_out5, RegLD);
  // Probe on reg1
  _16_bit_Register r1 (.LOAD(and_3_out), .CLK(Clock), .DATA(Data), .OUT(reg1));
  _16_bit_Register r5 (.LOAD(and_4_out), .CLK(Clock), .DATA(Data), .OUT(reg5));
  and and_5 (and_5_out, decoder_1_out2, RegLD);
  and and_6 (and_6_out, decoder_1_out6, RegLD);
  _16_bit_Register r2 (.LOAD(and_5_out), .CLK(Clock), .DATA(Data), .OUT(reg2));
  _16_bit_Register r6 (.LOAD(and_6_out), .CLK(Clock), .DATA(Data), .OUT(reg6));
  and and_7 (and_7_out, decoder_1_out3, RegLD);
  // Probe on reg3
  and and_8 (and_8_out, decoder_1_out7, RegLD);
  _16_bit_Register r3 (.LOAD(and_7_out), .CLK(Clock), .DATA(Data), .OUT(reg3));
  _16_bit_Register r7 (.LOAD(and_8_out), .CLK(Clock), .DATA(multiplexer_1_out), .OUT(reg7));
  Adder #(.width(16)) adder_1 (.a(reg7), .b(16'h1), .out(adder_1_out));  // open: cin, cout
  Subtractor #(.width(16)) subtractor_1 (.a(reg7), .b(16'h1), .out(subtractor_1_out));  // open: bin, bout
  Multiplexer #(.select(2), .width(16), .enable("false")) multiplexer_1 (
    .in0(Data), .in1(adder_1_out), .in2(subtractor_1_out), .in3(subtractor_1_out), .out(multiplexer_1_out),
    .sel({Sp_minus_minus, Sp_plus_plus}));
endmodule

module _12to16_Extender (
  input  [11:0] Input,
  output [15:0] Extended_Value
);


  assign Extended_Value = {Input, 4'b0000};
endmodule
